// Logisim project SoC.circ as structural Verilog: 18 circuits, main circuit SoC
module SoC (
  input  \清屏信号 ,
  input  \清空缓存 
);

  wire busmodel_1_ioen, busmodel_1_memr, busmodel_1_memw, busmodel_1_out_8, clk, dmemcache_1_miss, halt,
       keyboard_1_avail, keyttydriver_1_clock, keyttydriver_1_ttyenable, Miss, not_1_out, or_1_out,
       three_stage_cpu_1_out_5, three_stage_cpu_1_out_6;
  wire [3:0] leddriver_1_displaydata_2, leddriver_1_displaydata_3, leddriver_1_displaydata_4,
       leddriver_1_displaydata_5;
  wire [6:0] keyboard_1_data, keyttydriver_1_ttydata;
  wire [11:0] busmodel_1_ioaddr12;
  wire [15:0] leddriver_1_displaydata, MissNumber, \总周期数 ;
  wire [31:0] busmodel_1_iowritedata, busmodel_1_memaddr, busmodel_1_memwritedata, busmodel_1_readdata,
       dmemcache_1_read_data, Instruction, keyttydriver_1_ioread, three_stage_cpu_1_out_16,
       three_stage_cpu_1_out_17, three_stage_cpu_1_out_18;

  // Probe on three_stage_cpu_1_out_16
  Clock #(.highDuration(1), .lowDuration(1)) clock_1 (.out(clk));
  // Probe on \总周期数 
  // Probe on MissNumber
  Hex_Digit_Display hex_digit_display_1 (.value(leddriver_1_displaydata_5));  // open: dp
  Hex_Digit_Display hex_digit_display_2 (.value(leddriver_1_displaydata_4));  // open: dp
  Hex_Digit_Display hex_digit_display_3 (.value(leddriver_1_displaydata_3));  // open: dp
  IMEM imem_1 (.Program_counter(three_stage_cpu_1_out_16), .Instruction(Instruction));
  // Probe on Instruction
  Hex_Digit_Display hex_digit_display_4 (.value(leddriver_1_displaydata[15:12]));  // open: dp
  Hex_Digit_Display hex_digit_display_5 (.value(leddriver_1_displaydata_2));  // open: dp
  LedDriver leddriver_1 (
    .IOWriteData(busmodel_1_iowritedata), .IOAddr12(busmodel_1_ioaddr12), .IOEn(busmodel_1_ioen),
    .DisplayData({leddriver_1_displaydata_5, leddriver_1_displaydata_4, leddriver_1_displaydata_3, leddriver_1_displaydata_2, leddriver_1_displaydata}),
    .in_4(clk));
  Hex_Digit_Display hex_digit_display_6 (.value(leddriver_1_displaydata[11:8]));  // open: dp
  Hex_Digit_Display hex_digit_display_7 (.value(leddriver_1_displaydata[7:4]));  // open: dp
  // Probe on Miss
  Hex_Digit_Display hex_digit_display_8 (.value(leddriver_1_displaydata[3:0]));  // open: dp
  // Probe on busmodel_1_iowritedata
  not not_1 (not_1_out, or_1_out);
  or or_1 (or_1_out, halt, Miss);
  Counter #(.width(16), .max('hffff), .ongoal("wrap"), .trigger("rising"), .behavior("old")) counter_1 (
    .count(not_1_out), .Q(\总周期数 ), .clk(clk));  // open: load, D, carry, clr, preset
  // Probe on busmodel_1_ioaddr12
  Three_stage_CPU three_stage_cpu_1 (
    .in_1(Instruction), .in_2(busmodel_1_readdata), .out_5(three_stage_cpu_1_out_5),
    .out_6(three_stage_cpu_1_out_6), .out_16(three_stage_cpu_1_out_16), .out_17(three_stage_cpu_1_out_17),
    .out_18(three_stage_cpu_1_out_18), .in_3(clk), .out_7(halt), .in_4(dmemcache_1_miss));  // open: out_8, out_9, out_10, out_11, out_12, out_13, out_14, out_15
  TTY #(.Char_bit_width(7), .rows(16), .cols(40), .trigger("rising")) tty_1 (
    .data(keyttydriver_1_ttydata), .clk(keyttydriver_1_clock), .we(keyttydriver_1_ttyenable), .clr(\清屏信号 ));
  BusModel busmodel_1 (
    .ReadData(busmodel_1_readdata), .IOEn(busmodel_1_ioen), .IOWriteData(busmodel_1_iowritedata),
    .IORead(keyttydriver_1_ioread), .WriteAddr(three_stage_cpu_1_out_17), .R(three_stage_cpu_1_out_5),
    .MemRead(dmemcache_1_read_data), .WriteData(three_stage_cpu_1_out_18), .IOAddr12(busmodel_1_ioaddr12),
    .MemAddr(busmodel_1_memaddr), .MemR(busmodel_1_memr), .MemWriteData(busmodel_1_memwritedata),
    .out_8(busmodel_1_out_8), .W(three_stage_cpu_1_out_6), .MemW(busmodel_1_memw));
  Keyboard #(.Char_bit_width(7), .buflen(32), .trigger("rising")) keyboard_1 (
    .clk(keyttydriver_1_clock), .re(1'b1), .clr(\清空缓存 ), .avail(keyboard_1_avail), .data(keyboard_1_data));
  KeyTTYDriver keyttydriver_1 (
    .TTYData(keyttydriver_1_ttydata), .IORead(keyttydriver_1_ioread), .IOAddr12(busmodel_1_ioaddr12),
    .TTYEnable(keyttydriver_1_ttyenable), .IOEn(busmodel_1_ioen), .IOWriteData(busmodel_1_iowritedata),
    .KeyValue(keyboard_1_data), .clk(clk), .clock(keyttydriver_1_clock), .in_2(busmodel_1_out_8),
    .KeyEn(keyboard_1_avail));
  DMEMCache dmemcache_1 (
    .Miss(dmemcache_1_miss), .Write_Data(busmodel_1_memwritedata), .clk(clk), .MissNubmer(MissNumber),
    .Read_En(busmodel_1_memr), .Read_Data(dmemcache_1_read_data), .Address(busmodel_1_memaddr),
    .Write_En(busmodel_1_memw));

  // Notes on the sheet:
  //   时钟
  //   总周期数
  //   Cache缺失次数
  //   7-Segment驱动
  //   I/O总线
  //   键盘
  //   TTY 终端
  //   TTY和Keyboard驱动
endmodule

module Three_stage_CPU (
  input  [31:0] in_1,
  input  [31:0] in_2,
  input  in_3,
  input  in_4,
  output out_5,
  output out_6,
  output out_7,
  output [31:0] out_8,
  output [31:0] out_9,
  output [31:0] out_10,
  output [31:0] out_11,
  output [31:0] out_12,
  output [31:0] out_13,
  output [31:0] out_14,
  output [31:0] out_15,
  output [31:0] out_16,
  output [31:0] out_17,
  output [31:0] out_18
);

  wire and_4_out, and_5_out, and_6_out, and_7_out, Branch, branch_1_breq, branch_1_brlt, comparator_1_eq,
       comparator_2_eq, comparator_3_eq, comparator_4_eq, comparator_5_eq, comparator_6_eq,
       controlmodel_1_regwrite, En, ForwardA, ForwardB, or_1_out, or_2_out, PCSel, register_1_q,
       register_2_q, undriven;
  wire [2:0] ImmSel;
  wire [3:0] controlmodel_1_memread, register_4_q;
  wire [3:2] register_5_q;
  wire [6:0] CNT_ID_EX_q, register_3_q;
  wire [6:1] controlmodel_1_beq;
  wire [9:0] controlmodel_1_aluop;
  wire [31:0] adder_1_out, adder_2_out, alumodel_1_result, immmodel_1_immdiate, Inst_ID_EX_q, Inst_IF_ID,
       Inst_WB, multiplexer_1_out, multiplexer_3_out, multiplexer_4_out, multiplexer_5_out,
       multiplexer_6_out, multiplexer_7_out, PC_EX, PC_EX_MEM_q, R1_ID_EX_q, R2_ID_EX_q,
       regfile_1_read_data_1, regfile_1_read_data_2;

  Adder #(.width(32)) adder_1 (.a(out_16), .b(32'h4), .out(adder_1_out));  // open: cin, cout
  Multiplexer #(.select(1), .width(32), .disabled("Z"), .enable("false")) multiplexer_1 (
    .in0(adder_1_out), .in1(alumodel_1_result), .out(multiplexer_1_out), .sel(Branch));
  Register #(.width(32), .trigger("rising"), .Select("low")) PC (
    .D(multiplexer_1_out), .en(En), .Q(out_16), .clk(in_3));  // open: clr
  Comparator #(.width(32), .mode("unsigned")) comparator_1 (
    .a(Inst_IF_ID), .b({32{1'b0}}), .eq(comparator_1_eq));  // open: gt, lt
  Comparator #(.width(32), .mode("unsigned")) comparator_2 (
    .a(Inst_WB), .b({32{1'b0}}), .eq(comparator_2_eq));  // open: gt, lt
  // Probe on adder_1_out
  // Probe on out_16
  // Probe on in_1
  nor nor_1 (En, comparator_1_eq, in_4);
  Pull_Resistor #(.pull(0)) pull_resistor_1 (.node(in_4));
  and and_1 (out_7, comparator_1_eq, comparator_2_eq);
  Multiplexer #(.select(1), .width(32), .disabled("Z"), .enable("false")) multiplexer_2 (
    .in0(in_1), .in1(32'h13), .out(Inst_IF_ID), .sel(Branch));
  // Probe on Inst_IF_ID
  Register #(.width(1), .trigger("rising"), .Select("low")) register_1 (
    .D(controlmodel_1_regwrite), .Q(register_1_q), .clk(in_3));  // open: en, clr
  ControlModel controlmodel_1 (
    .Instruction(Inst_IF_ID), .ALUSelB(controlmodel_1_aluop[4]), .PCSel(PCSel),
    .RegWrite(controlmodel_1_regwrite), .ALUSelA(controlmodel_1_aluop[5]),
    .MemWrite(controlmodel_1_memread[1]), .ImmSel(controlmodel_1_aluop[9:7]),
    .ALUOP(controlmodel_1_aluop[3:0]), .BrUN(controlmodel_1_aluop[6]), .WBSel(controlmodel_1_memread[3:2]),
    .MemRead(controlmodel_1_memread[0]), .BEQ(controlmodel_1_beq[1]), .BNE(controlmodel_1_beq[2]),
    .BGE(controlmodel_1_beq[5]), .BLT(controlmodel_1_beq[3]), .BLTU(controlmodel_1_beq[4]),
    .BGEU(controlmodel_1_beq[6]));
  Register #(.width(1), .trigger("rising"), .Select("low")) register_2 (
    .D(register_1_q), .Q(register_2_q), .clk(in_3));  // open: en, clr
  // Probe on out_8
  // Probe on out_10
  Comparator #(.width(5), .mode("unsigned")) comparator_3 (
    .a(Inst_IF_ID[24:20]), .b(Inst_WB[11:7]), .eq(comparator_3_eq));  // open: gt, lt
  Comparator #(.width(5), .mode("unsigned")) comparator_4 (
    .a(Inst_IF_ID[19:15]), .b(Inst_WB[11:7]), .eq(comparator_4_eq));  // open: gt, lt
  Register #(.width(7), .trigger("rising"), .Select("low")) register_3 (
    .D({controlmodel_1_beq, PCSel}), .Q(register_3_q), .clk(in_3));  // open: en, clr
  Register #(.width(10), .trigger("rising"), .Select("low")) CNT_ID_EX (
    .D(controlmodel_1_aluop), .Q({ImmSel, CNT_ID_EX_q}), .clk(in_3));  // open: en, clr
  // Probe on out_11
  // Probe on out_12
  Comparator #(.width(5), .mode("unsigned")) comparator_5 (
    .a(Inst_IF_ID[24:20]), .b({5{1'b0}}), .eq(comparator_5_eq));  // open: gt, lt
  Comparator #(.width(5), .mode("unsigned")) comparator_6 (
    .a(Inst_IF_ID[19:15]), .b({5{1'b0}}), .eq(comparator_6_eq));  // open: gt, lt
  // Probe on out_13
  // Probe on out_14
  and and_2 (ForwardB, ~comparator_5_eq, comparator_3_eq);  // AND_Gate
  and and_3 (ForwardA, ~comparator_6_eq, comparator_4_eq);  // AND_Gate
  RegFile regfile_1 (
    .rs1(Inst_IF_ID[19:15]), .rs2(Inst_IF_ID[24:20]), .rd(Inst_WB[11:7]), .Write_Data(multiplexer_7_out),
    .RegWEn(register_2_q), .clk(in_3), .Read_Data_1(regfile_1_read_data_1),
    .Read_Data_2(regfile_1_read_data_2), .ra(out_8), .sp(out_9), .t0(out_10), .t1(out_11), .t2(out_12),
    .s0(out_13), .s1(out_14), .a0(out_15));
  Register #(.width(32), .trigger("rising"), .Select("low")) Inst_ID_EX (
    .D(Inst_IF_ID), .en(1'b1), .Q(Inst_ID_EX_q), .clk(in_3));  // open: clr
  Register #(.width(32), .trigger("rising"), .Select("low")) PC_ID_EX (
    .D(out_16), .en(1'b1), .Q(PC_EX), .clk(in_3));  // open: clr
  Register #(.width(32), .trigger("rising"), .Select("low")) R1_ID_EX (
    .D(regfile_1_read_data_1), .en(undriven), .Q(R1_ID_EX_q), .clk(in_3));  // open: clr
  Register #(.width(32), .trigger("rising"), .Select("low")) R2_ID_EX (
    .D(regfile_1_read_data_2), .en(1'b1), .Q(R2_ID_EX_q), .clk(in_3));  // open: clr
  Multiplexer #(.select(1), .width(32), .disabled("Z"), .enable("false")) multiplexer_3 (
    .in0(R1_ID_EX_q), .in1(out_17), .out(multiplexer_3_out), .sel(ForwardA));
  Multiplexer #(.select(1), .width(32), .disabled("Z"), .enable("false")) multiplexer_4 (
    .in0(R2_ID_EX_q), .in1(out_17), .out(multiplexer_4_out), .sel(ForwardB));
  ImmModel immmodel_1 (.Immdiate(immmodel_1_immdiate), .InstructionType(ImmSel), .INSTRUCTION(Inst_ID_EX_q));
  or or_1 (or_1_out, register_3_q[3], register_3_q[4]);
  or or_2 (or_2_out, register_3_q[5], register_3_q[6]);
  Branch branch_1 (
    .BrEQ(branch_1_breq), .RS2(multiplexer_4_out), .BrUN(CNT_ID_EX_q[6]), .BrLT(branch_1_brlt),
    .RS1(multiplexer_3_out));
  Multiplexer #(.select(1), .width(32), .disabled("Z"), .enable("false")) multiplexer_5 (
    .in0(multiplexer_3_out), .in1(PC_EX), .out(multiplexer_5_out), .sel(CNT_ID_EX_q[5]));
  Multiplexer #(.select(1), .width(32), .disabled("Z"), .enable("false")) multiplexer_6 (
    .in0(multiplexer_4_out), .in1(immmodel_1_immdiate), .out(multiplexer_6_out), .sel(CNT_ID_EX_q[4]));
  Register #(.width(32), .trigger("rising"), .Select("low")) Inst_EX_MEM (
    .D(Inst_ID_EX_q), .en(1'b1), .Q(Inst_WB), .clk(in_3));  // open: clr
  and and_4 (and_4_out, branch_1_breq, register_3_q[1]);
  and and_5 (and_5_out, ~branch_1_breq, register_3_q[2]);  // AND_Gate
  and and_6 (and_6_out, branch_1_brlt, or_1_out);
  and and_7 (and_7_out, ~branch_1_brlt, or_2_out);  // AND_Gate
  // Probe on CNT_ID_EX_q[3:0]
  AluModel alumodel_1 (
    .Result(alumodel_1_result), .ALUSel(CNT_ID_EX_q[3:0]), .B(multiplexer_6_out), .A(multiplexer_5_out));
  // Probe on alumodel_1_result
  or or_3 (Branch, register_3_q[0], and_4_out, and_5_out, and_6_out, and_7_out);
  Register #(.width(4), .trigger("rising"), .Select("low")) register_4 (
    .D(controlmodel_1_memread), .Q(register_4_q), .clk(in_3));  // open: en, clr
  Register #(.width(4), .trigger("rising"), .Select("low")) register_5 (
    .D(register_4_q), .Q({register_5_q, out_6, out_5}), .clk(in_3));  // open: en, clr
  Register #(.width(32), .trigger("rising"), .Select("low")) PC_EX_MEM (
    .D(PC_EX), .en(1'b1), .Q(PC_EX_MEM_q), .clk(in_3));  // open: clr
  // Probe on out_17
  Register #(.width(32), .trigger("rising"), .Select("low")) ALU_EX_MEM (
    .D(alumodel_1_result), .en(1'b1), .Q(out_17), .clk(in_3));  // open: clr
  Register #(.width(32), .trigger("rising"), .Select("low")) R2_EX_MEM (
    .D(multiplexer_4_out), .en(1'b1), .Q(out_18), .clk(in_3));  // open: clr
  // Probe on out_18
  Adder #(.width(32)) adder_2 (.a(PC_EX_MEM_q), .b(32'h4), .out(adder_2_out));  // open: cin, cout
  // Probe on register_5_q
  // Probe on in_2
  Multiplexer #(.select(2), .width(32), .disabled("Z"), .enable("false")) multiplexer_7 (
    .in0(adder_2_out), .in1(out_17), .in2(in_2), .out(multiplexer_7_out), .sel(register_5_q));  // open: in3
  // Probe on multiplexer_7_out

  // Other names for the same wires on the sheet: MemR = out_5; MemW = out_6; a0[31:0] = out_15; clk = in_3;
  //   fetch_addr[31:0] = out_16; halt = out_7; Instruction[31:0] = in_1; Miss = in_4; ra[31:0] = out_8;
  //   ReadData[31:0] = in_2; s0[31:0] = out_13; s1[31:0] = out_14; sp[31:0] = out_9; t0[31:0] = out_10;
  //   t1[31:0] = out_11; t2[31:0] = out_12; ALUResult[31:0] = out_17; WriteAddr[31:0] = out_17;
  //   WriteData[31:0] = out_18

  // Notes on the sheet:
  //   PC
  //   PC+4
  //   ALU_Result
  //   ALU_Result
  //   输入引脚区
  //   输出引脚区
  //   ALU_Result
  //   PC+4
  //   WriteData
  //   WBSel
endmodule

module cpu (
  input  [31:0] in_1,
  input  [31:0] in_2,
  input  in_3,
  input  in_4,
  output out_5,
  output out_6,
  output out_7,
  output [31:0] out_8,
  output [31:0] out_9,
  output [31:0] out_10,
  output [31:0] out_11,
  output [31:0] out_12,
  output [31:0] out_13,
  output [31:0] out_14,
  output [31:0] out_15,
  output [31:0] out_16,
  output [31:0] out_17,
  output [31:0] out_18
);

  wire and_1_out, and_2_out, and_3_out, and_4_out, Branch, branch_1_breq, branch_1_brlt,
       controlmodel_1_alusela, controlmodel_1_aluselb, controlmodel_1_beq, controlmodel_1_bge,
       controlmodel_1_bgeu, controlmodel_1_blt, controlmodel_1_bltu, controlmodel_1_bne, controlmodel_1_brun,
       controlmodel_1_pcsel, controlmodel_1_regwrite, En, or_1_out, or_2_out;
  wire [1:0] controlmodel_1_wbsel;
  wire [2:0] controlmodel_1_immsel;
  wire [3:0] controlmodel_1_aluop;
  wire [31:0] adder_1_out, immmodel_1_immdiate, multiplexer_1_out, multiplexer_2_out, multiplexer_3_out,
       multiplexer_4_out, regfile_1_read_data_1;

  Adder #(.width(32)) adder_1 (.a(out_16), .b(32'h4), .out(adder_1_out));  // open: cin, cout
  Multiplexer #(.select(1), .width(32), .disabled("Z"), .enable("false")) multiplexer_1 (
    .in0(adder_1_out), .in1(out_17), .out(multiplexer_1_out), .sel(Branch));
  Comparator #(.width(32), .mode("unsigned")) comparator_1 (.a(in_1), .b({32{1'b0}}), .eq(out_7));  // open: gt, lt
  Register #(.width(32), .trigger("rising"), .Select("low")) PC (
    .D(multiplexer_1_out), .en(En), .Q(out_16), .clk(in_3));  // open: clr
  // Probe on adder_1_out
  // Probe on out_16
  nor nor_1 (En, out_7, in_4);
  Pull_Resistor #(.pull(0)) pull_resistor_1 (.node(in_4));
  // Probe on in_1
  ControlModel controlmodel_1 (
    .Instruction(in_1), .ALUSelB(controlmodel_1_aluselb), .PCSel(controlmodel_1_pcsel),
    .RegWrite(controlmodel_1_regwrite), .ALUSelA(controlmodel_1_alusela), .MemWrite(out_6),
    .ImmSel(controlmodel_1_immsel), .ALUOP(controlmodel_1_aluop), .BrUN(controlmodel_1_brun),
    .WBSel(controlmodel_1_wbsel), .MemRead(out_5), .BEQ(controlmodel_1_beq), .BNE(controlmodel_1_bne),
    .BGE(controlmodel_1_bge), .BLT(controlmodel_1_blt), .BLTU(controlmodel_1_bltu), .BGEU(controlmodel_1_bgeu));
  ImmModel immmodel_1 (.Immdiate(immmodel_1_immdiate), .InstructionType(controlmodel_1_immsel), .INSTRUCTION(in_1));
  RegFile regfile_1 (
    .rs1(in_1[19:15]), .rs2(in_1[24:20]), .rd(in_1[11:7]), .Write_Data(multiplexer_4_out),
    .RegWEn(controlmodel_1_regwrite), .clk(in_3), .Read_Data_1(regfile_1_read_data_1), .Read_Data_2(out_18),
    .ra(out_8), .sp(out_9), .t0(out_10), .t1(out_11), .t2(out_12), .s0(out_13), .s1(out_14), .a0(out_15));
  or or_1 (or_1_out, controlmodel_1_blt, controlmodel_1_bltu);
  or or_2 (or_2_out, controlmodel_1_bge, controlmodel_1_bgeu);
  Branch branch_1 (
    .BrEQ(branch_1_breq), .RS2(out_18), .BrUN(controlmodel_1_brun), .BrLT(branch_1_brlt),
    .RS1(regfile_1_read_data_1));
  Multiplexer #(.select(1), .width(32), .disabled("Z"), .enable("false")) multiplexer_2 (
    .in0(regfile_1_read_data_1), .in1(out_16), .out(multiplexer_2_out), .sel(controlmodel_1_alusela));
  Multiplexer #(.select(1), .width(32), .disabled("Z"), .enable("false")) multiplexer_3 (
    .in0(out_18), .in1(immmodel_1_immdiate), .out(multiplexer_3_out), .sel(controlmodel_1_aluselb));
  and and_1 (and_1_out, branch_1_breq, controlmodel_1_beq);
  and and_2 (and_2_out, ~branch_1_breq, controlmodel_1_bne);  // AND_Gate
  and and_3 (and_3_out, branch_1_brlt, or_1_out);
  and and_4 (and_4_out, ~branch_1_brlt, or_2_out);  // AND_Gate
  or or_3 (Branch, controlmodel_1_pcsel, and_1_out, and_2_out, and_3_out, and_4_out);
  // Probe on out_17
  AluModel alumodel_1 (.Result(out_17), .ALUSel(controlmodel_1_aluop), .B(multiplexer_3_out), .A(multiplexer_2_out));
  // Probe on out_18
  // Probe on in_2
  Multiplexer #(.select(2), .width(32), .disabled("Z"), .enable("false")) multiplexer_4 (
    .in0(adder_1_out), .in1(out_17), .in2(in_2), .out(multiplexer_4_out), .sel(controlmodel_1_wbsel));  // open: in3

  // Other names for the same wires on the sheet: a0[31:0] = out_15; clk = in_3; fetch_addr[31:0] = out_16;
  //   halt = out_7; Instruction[31:0] = in_1; MemR = out_5; MemW = out_6; Miss = in_4; ra[31:0] = out_8;
  //   ReadData[31:0] = in_2; s0[31:0] = out_13; s1[31:0] = out_14; sp[31:0] = out_9; t0[31:0] = out_10;
  //   t1[31:0] = out_11; t2[31:0] = out_12; WriteAddr[31:0] = out_17; WriteData[31:0] = out_18

  // Notes on the sheet:
  //   PC
  //   PC+4
  //   ALU_Result
  //   ALU_Result
  //   输入引脚区
  //   请勿增改引脚，请勿修改子电路封装
  //   输出引脚区
  //   ALU_Result
  //   PC+4
  //   WriteData
  //   WBSel
endmodule

module RegFile (
  input  [4:0] rs1,
  input  [4:0] rs2,
  input  [4:0] rd,
  input  [31:0] Write_Data,
  input  RegWEn,
  input  clk,
  output [31:0] ra,
  output [31:0] sp,
  output [31:0] t0,
  output [31:0] t1,
  output [31:0] t2,
  output [31:0] s0,
  output [31:0] s1,
  output [31:0] a0,
  output [31:0] Read_Data_1,
  output [31:0] Read_Data_2
);

  wire write_en1, write_en2, write_en3, write_en4, write_en5, write_en6, write_en7, write_en8, write_en9,
       write_en10, write_en11, write_en12, write_en13, write_en14, write_en15, write_en16, write_en17,
       write_en18, write_en19, write_en20, write_en21, write_en22, write_en23, write_en24, write_en25,
       write_en26, write_en27, write_en28, write_en29, write_en30, write_en31;
  wire [31:0] x3, x4, x11, x12, x13, x14, x15, x16, x17, x18, x19, x20, x21, x22, x23, x24, x25, x26, x27,
       x28, x29, x30, x31;

  Pull_Resistor #(.pull(0)) pull_resistor_1 (.node(write_en1));
  Register #(.width(32), .trigger("rising"), .Select("low")) register_1 (
    .D(Write_Data), .en(write_en8), .Q(s0), .clk(clk));  // open: clr
  Register #(.width(32), .trigger("rising"), .Select("low")) register_2 (
    .D(Write_Data), .en(write_en16), .Q(x16), .clk(clk));  // open: clr
  Register #(.width(32), .trigger("rising"), .Select("low")) register_3 (
    .D(Write_Data), .en(write_en24), .Q(x24), .clk(clk));  // open: clr
  Pull_Resistor #(.pull(0)) pull_resistor_2 (.node(write_en3));
  Pull_Resistor #(.pull(0)) pull_resistor_3 (.node(write_en2));
  Pull_Resistor #(.pull(0)) pull_resistor_4 (.node(write_en4));
  Pull_Resistor #(.pull(0)) pull_resistor_5 (.node(write_en5));
  // Probe on ra
  Register #(.width(32), .trigger("rising"), .Select("low")) register_4 (
    .D(Write_Data), .en(write_en1), .Q(ra), .clk(clk));  // open: clr
  Register #(.width(32), .trigger("rising"), .Select("low")) register_5 (
    .D(Write_Data), .en(write_en9), .Q(s1), .clk(clk));  // open: clr
  Register #(.width(32), .trigger("rising"), .Select("low")) register_6 (
    .D(Write_Data), .en(write_en17), .Q(x17), .clk(clk));  // open: clr
  Register #(.width(32), .trigger("rising"), .Select("low")) register_7 (
    .D(Write_Data), .en(write_en25), .Q(x25), .clk(clk));  // open: clr
  Pull_Resistor #(.pull(0)) pull_resistor_6 (.node(write_en6));
  Pull_Resistor #(.pull(0)) pull_resistor_7 (.node(write_en7));
  Pull_Resistor #(.pull(0)) pull_resistor_8 (.node(write_en8));
  Pull_Resistor #(.pull(0)) pull_resistor_9 (.node(write_en9));
  // Probe on Write_Data
  // Probe on write_en18
  Pull_Resistor #(.pull(0)) pull_resistor_10 (.node(write_en11));
  Pull_Resistor #(.pull(0)) pull_resistor_11 (.node(write_en10));
  Register #(.width(32), .trigger("rising"), .Select("low")) register_8 (
    .D(Write_Data), .en(write_en2), .Q(sp), .clk(clk));  // open: clr
  Register #(.width(32), .trigger("rising"), .Select("low")) register_9 (
    .D(Write_Data), .en(write_en10), .Q(a0), .clk(clk));  // open: clr
  Register #(.width(32), .trigger("rising"), .Select("low")) register_10 (
    .D(Write_Data), .en(write_en18), .Q(x18), .clk(clk));  // open: clr
  // Probe on x18
  Register #(.width(32), .trigger("rising"), .Select("low")) register_11 (
    .D(Write_Data), .en(write_en26), .Q(x26), .clk(clk));  // open: clr
  Pull_Resistor #(.pull(0)) pull_resistor_12 (.node(write_en12));
  Pull_Resistor #(.pull(0)) pull_resistor_13 (.node(write_en13));
  Pull_Resistor #(.pull(0)) pull_resistor_14 (.node(write_en14));
  Pull_Resistor #(.pull(0)) pull_resistor_15 (.node(write_en15));
  Register #(.width(32), .trigger("rising"), .Select("low")) register_12 (
    .D(Write_Data), .en(write_en3), .Q(x3), .clk(clk));  // open: clr
  Register #(.width(32), .trigger("rising"), .Select("low")) register_13 (
    .D(Write_Data), .en(write_en11), .Q(x11), .clk(clk));  // open: clr
  Register #(.width(32), .trigger("rising"), .Select("low")) register_14 (
    .D(Write_Data), .en(write_en19), .Q(x19), .clk(clk));  // open: clr
  Register #(.width(32), .trigger("rising"), .Select("low")) register_15 (
    .D(Write_Data), .en(write_en27), .Q(x27), .clk(clk));  // open: clr
  Pull_Resistor #(.pull(0)) pull_resistor_16 (.node(write_en16));
  Pull_Resistor #(.pull(0)) pull_resistor_17 (.node(write_en17));
  Pull_Resistor #(.pull(0)) pull_resistor_18 (.node(write_en18));
  Pull_Resistor #(.pull(0)) pull_resistor_19 (.node(write_en19));
  Register #(.width(32), .trigger("rising"), .Select("low")) register_16 (
    .D(Write_Data), .en(write_en4), .Q(x4), .clk(clk));  // open: clr
  Register #(.width(32), .trigger("rising"), .Select("low")) register_17 (
    .D(Write_Data), .en(write_en12), .Q(x12), .clk(clk));  // open: clr
  Register #(.width(32), .trigger("rising"), .Select("low")) register_18 (
    .D(Write_Data), .en(write_en20), .Q(x20), .clk(clk));  // open: clr
  Register #(.width(32), .trigger("rising"), .Select("low")) register_19 (
    .D(Write_Data), .en(write_en28), .Q(x28), .clk(clk));  // open: clr
  Pull_Resistor #(.pull(0)) pull_resistor_20 (.node(write_en20));
  Pull_Resistor #(.pull(0)) pull_resistor_21 (.node(write_en21));
  Pull_Resistor #(.pull(0)) pull_resistor_22 (.node(write_en23));
  Pull_Resistor #(.pull(0)) pull_resistor_23 (.node(write_en22));
  Decoder #(.select(5), .tristate("false"), .disabled("Z"), .enable("true")) decoder_1 (
    .out1(write_en1), .out2(write_en2), .out3(write_en3), .out4(write_en4), .out5(write_en5),
    .out6(write_en6), .out7(write_en7), .out8(write_en8), .out9(write_en9), .out10(write_en10),
    .out11(write_en11), .out12(write_en12), .out13(write_en13), .out14(write_en14), .out15(write_en15),
    .out16(write_en16), .out17(write_en17), .out18(write_en18), .out19(write_en19), .out20(write_en20),
    .out21(write_en21), .out22(write_en22), .out23(write_en23), .out24(write_en24), .out25(write_en25),
    .out26(write_en26), .out27(write_en27), .out28(write_en28), .out29(write_en29), .out30(write_en30),
    .out31(write_en31), .sel(rd), .en(RegWEn));  // open: out0
  Register #(.width(32), .trigger("rising"), .Select("low")) register_20 (
    .D(Write_Data), .en(write_en5), .Q(t0), .clk(clk));  // open: clr
  Register #(.width(32), .trigger("rising"), .Select("low")) register_21 (
    .D(Write_Data), .en(write_en13), .Q(x13), .clk(clk));  // open: clr
  Register #(.width(32), .trigger("rising"), .Select("low")) register_22 (
    .D(Write_Data), .en(write_en21), .Q(x21), .clk(clk));  // open: clr
  Register #(.width(32), .trigger("rising"), .Select("low")) register_23 (
    .D(Write_Data), .en(write_en29), .Q(x29), .clk(clk));  // open: clr
  Pull_Resistor #(.pull(0)) pull_resistor_24 (.node(write_en24));
  // Probe on rd
  Pull_Resistor #(.pull(0)) pull_resistor_25 (.node(write_en25));
  Pull_Resistor #(.pull(0)) pull_resistor_26 (.node(write_en27));
  Pull_Resistor #(.pull(0)) pull_resistor_27 (.node(write_en26));
  Pull_Resistor #(.pull(0)) pull_resistor_28 (.node(write_en28));
  Register #(.width(32), .trigger("rising"), .Select("low")) register_24 (
    .D(Write_Data), .en(write_en6), .Q(t1), .clk(clk));  // open: clr
  Register #(.width(32), .trigger("rising"), .Select("low")) register_25 (
    .D(Write_Data), .en(write_en14), .Q(x14), .clk(clk));  // open: clr
  Register #(.width(32), .trigger("rising"), .Select("low")) register_26 (
    .D(Write_Data), .en(write_en22), .Q(x22), .clk(clk));  // open: clr
  Register #(.width(32), .trigger("rising"), .Select("low")) register_27 (
    .D(Write_Data), .en(write_en30), .Q(x30), .clk(clk));  // open: clr
  // Probe on x30
  Pull_Resistor #(.pull(0)) pull_resistor_29 (.node(write_en29));
  Pull_Resistor #(.pull(0)) pull_resistor_30 (.node(write_en30));
  Pull_Resistor #(.pull(0)) pull_resistor_31 (.node(write_en31));
  // Probe on Read_Data_1
  // Probe on rs1
  Register #(.width(32), .trigger("rising"), .Select("low")) register_28 (
    .D(Write_Data), .en(write_en7), .Q(t2), .clk(clk));  // open: clr
  Register #(.width(32), .trigger("rising"), .Select("low")) register_29 (
    .D(Write_Data), .en(write_en15), .Q(x15), .clk(clk));  // open: clr
  Register #(.width(32), .trigger("rising"), .Select("low")) register_30 (
    .D(Write_Data), .en(write_en23), .Q(x23), .clk(clk));  // open: clr
  Register #(.width(32), .trigger("rising"), .Select("low")) register_31 (
    .D(Write_Data), .en(write_en31), .Q(x31), .clk(clk));  // open: clr
  Multiplexer #(.select(5), .width(32), .disabled("Z"), .enable("false")) multiplexer_1 (
    .in0({32{1'b0}}), .in1(ra), .in2(sp), .in3(x3), .in4(x4), .in5(t0), .in6(t1), .in7(t2), .in8(s0),
    .in9(s1), .in10(a0), .in11(x11), .in12(x12), .in13(x13), .in14(x14), .in15(x15), .in16(x16), .in17(x17),
    .in18(x18), .in19(x19), .in20(x20), .in21(x21), .in22(x22), .in23(x23), .in24(x24), .in25(x25),
    .in26(x26), .in27(x27), .in28(x28), .in29(x29), .in30(x30), .in31(x31), .out(Read_Data_1), .sel(rs1));
  // Probe on Read_Data_2
  // Probe on rs2
  Multiplexer #(.select(5), .width(32), .disabled("Z"), .enable("false")) multiplexer_2 (
    .in0({32{1'b0}}), .in1(ra), .in2(sp), .in3(x3), .in4(x4), .in5(t0), .in6(t1), .in7(t2), .in8(s0),
    .in9(s1), .in10(a0), .in11(x11), .in12(x12), .in13(x13), .in14(x14), .in15(x15), .in16(x16), .in17(x17),
    .in18(x18), .in19(x19), .in20(x20), .in21(x21), .in22(x22), .in23(x23), .in24(x24), .in25(x25),
    .in26(x26), .in27(x27), .in28(x28), .in29(x29), .in30(x30), .in31(x31), .out(Read_Data_2), .sel(rs2));

  // Other names for the same wires on the sheet: read_data1[31:0] = Read_Data_1; read_data2[31:0] = Read_Data_2;
  //   read_reg1[4:0] = rs1; read_reg2[4:0] = rs2; write_en = RegWEn; write_reg[4:0] = rd; x1[31:0] = ra;
  //   x2[31:0] = sp; x5[31:0] = t0; x6[31:0] = t1; x7[31:0] = t2; x8[31:0] = s0; x9[31:0] = s1; x10[31:0] = a0

  // Notes on the sheet:
  //   INPUTS to your circuit
  //   DON'T CHANGE THE LOCATIONS OF THE INPUTS AND OUTPUTS!
  //   These are DEBUG/TEST outputs from your circuit.
  //   OUTPUTS from your circuit
endmodule

module ControlModel (
  input  [31:0] Instruction,
  output BrUN,
  output RegWrite,
  output MemWrite,
  output MemRead,
  output PCSel,
  output [2:0] ImmSel,
  output ALUSelA,
  output ALUSelB,
  output [1:0] WBSel,
  output [3:0] ALUOP,
  output BEQ,
  output BLT,
  output BNE,
  output BLTU,
  output BGE,
  output BGEU
);

  wire and_5_out, and_10_out, comparator_3_eq, comparator_4_eq, comparator_5_eq, comparator_6_eq,
       comparator_7_eq, comparator_8_eq, comparator_13_eq, comparator_14_eq, comparator_15_eq,
       comparator_16_eq, comparator_17_eq, comparator_18_eq, comparator_19_eq, comparator_20_eq, IType, JALR,
       Load, or_2_out, or_3_out, or_4_out, or_5_out, or_11_out, or_12_out, RType, SBType, UJType, UType;
  wire [1:0] priority_encoder_4_out;
  wire [2:0] priority_encoder_3_out;
  wire [3:0] AOP_I, AOP_R, rom_2_data;

  Comparator #(.width(7), .mode("unsigned")) comparator_1 (
    .a(Instruction[6:0]), .b(7'b0110011), .eq(RType));  // open: gt, lt
  Comparator #(.width(7), .mode("unsigned")) comparator_2 (
    .a(Instruction[6:0]), .b(7'b0000011), .eq(MemRead));  // open: gt, lt
  Comparator #(.width(7), .mode("unsigned")) comparator_3 (
    .a(Instruction[6:0]), .b(7'b1100111), .eq(comparator_3_eq));  // open: gt, lt
  Comparator #(.width(7), .mode("unsigned")) comparator_4 (
    .a(Instruction[6:0]), .b(7'b0010011), .eq(comparator_4_eq));  // open: gt, lt
  Comparator #(.width(7), .mode("unsigned")) comparator_5 (
    .a(Instruction[6:0]), .b(7'b0000011), .eq(comparator_5_eq));  // open: gt, lt
  and and_1 (Load, comparator_5_eq, IType);
  Comparator #(.width(3), .mode("unsigned")) comparator_6 (
    .a(Instruction[14:12]), .b(3'b000), .eq(comparator_6_eq));  // open: gt, lt
  Comparator #(.width(3), .mode("unsigned")) comparator_7 (
    .a(Instruction[14:12]), .b(3'b001), .eq(comparator_7_eq));  // open: gt, lt
  Comparator #(.width(3), .mode("unsigned")) comparator_8 (
    .a(Instruction[14:12]), .b(3'b101), .eq(comparator_8_eq));  // open: gt, lt
  or or_1 (IType, MemRead, comparator_3_eq, comparator_4_eq);
  and and_2 (BEQ, comparator_6_eq, SBType);
  and and_3 (BNE, comparator_7_eq, SBType);
  and and_4 (BGE, comparator_8_eq, SBType);
  and and_5 (and_5_out, IType, ~JALR);  // AND_Gate
  Comparator #(.width(7), .mode("unsigned")) comparator_9 (
    .a(Instruction[6:0]), .b(7'b0110111), .eq(UType));  // open: gt, lt
  Comparator #(.width(7), .mode("unsigned")) comparator_10 (
    .a(Instruction[6:0]), .b(7'b1101111), .eq(UJType));  // open: gt, lt
  Comparator #(.width(7), .mode("unsigned")) comparator_11 (
    .a(Instruction[6:0]), .b(7'b0100011), .eq(MemWrite));  // open: gt, lt
  Comparator #(.width(7), .mode("unsigned")) comparator_12 (
    .a(Instruction[6:0]), .b(7'b1100011), .eq(SBType));  // open: gt, lt
  Comparator #(.width(7), .mode("unsigned")) comparator_13 (
    .a(Instruction[6:0]), .b(7'b1100111), .eq(comparator_13_eq));  // open: gt, lt
  Comparator #(.width(3), .mode("unsigned")) comparator_14 (
    .a(Instruction[14:12]), .b(3'b100), .eq(comparator_14_eq));  // open: gt, lt
  Comparator #(.width(3), .mode("unsigned")) comparator_15 (
    .a(Instruction[14:12]), .b(3'b110), .eq(comparator_15_eq));  // open: gt, lt
  Comparator #(.width(3), .mode("unsigned")) comparator_16 (
    .a(Instruction[14:12]), .b(3'b111), .eq(comparator_16_eq));  // open: gt, lt
  and and_6 (JALR, comparator_13_eq, IType);
  or or_2 (or_2_out, RType, and_5_out, UType);
  and and_7 (BLT, comparator_14_eq, SBType);
  and and_8 (BLTU, comparator_15_eq, SBType);
  and and_9 (BGEU, comparator_16_eq, SBType);
  or or_3 (or_3_out, UJType, JALR);
  or or_4 (or_4_out, or_3_out, or_2_out, Load);
  Priority_Encoder #(.select(3), .disabled("Z")) priority_encoder_1 (
    .in0(IType), .in1(MemWrite), .in2(SBType), .in3(UType), .in4(UJType), .out(ImmSel), .en_in(or_5_out));  // open: in5, in6, in7, gs, en_out
  or or_5 (or_5_out, IType, MemWrite, SBType, UType, UJType);
  Priority_Encoder #(.select(2), .disabled("Z")) priority_encoder_2 (
    .in0(or_3_out), .in1(or_2_out), .in2(Load), .out(WBSel), .en_in(or_4_out));  // open: in3, gs, en_out
  Pull_Resistor #(.pull(0)) pull_resistor_1 (.node(WBSel));
  or or_6 (BrUN, BLTU, BGEU);
  or or_7 (RegWrite, RType, IType, UType, UJType);
  or or_8 (PCSel, JALR, UJType);
  Pull_Resistor #(.pull(0)) pull_resistor_2 (.node(ImmSel));
  or or_9 (ALUSelA, SBType, UJType);
  or or_10 (ALUSelB, IType, MemWrite, SBType, UType, UJType);
  // Probe on PCSel
  // Probe on Instruction[6:0]
  Comparator #(.width(7), .mode("unsigned")) comparator_17 (
    .a(7'b0010011), .b(Instruction[6:0]), .eq(comparator_17_eq));  // open: gt, lt
  Comparator #(.width(3), .mode("unsigned")) comparator_18 (
    .a(3'b101), .b(Instruction[14:12]), .eq(comparator_18_eq));  // open: gt, lt
  Comparator #(.width(7), .mode("unsigned")) comparator_19 (
    .a(7'b0100000), .b(Instruction[31:25]), .eq(comparator_19_eq));  // open: gt, lt
  Comparator #(.width(7), .mode("unsigned")) comparator_20 (
    .a(7'b0000011), .b(Instruction[6:0]), .eq(comparator_20_eq));  // open: gt, lt
  // Probe on comparator_20_eq
  ROM #(.addrWidth(10), .dataWidth(4), .Select("high")) rom_1 (
    .addr({Instruction[14:12], Instruction[31:25]}), .data(AOP_R));
  ROM #(.addrWidth(3), .dataWidth(4), .Select("high")) rom_2 (.addr(Instruction[14:12]), .data(rom_2_data));
  // Probe on and_10_out
  and and_10 (and_10_out, comparator_17_eq, comparator_18_eq, comparator_19_eq);
  or or_11 (or_11_out, and_10_out, comparator_20_eq);
  Priority_Encoder #(.select(3), .disabled("Z")) priority_encoder_3 (
    .in0(RType), .in1(IType), .in2(MemWrite), .in3(SBType), .in4(UType), .in5(UJType),
    .out(priority_encoder_3_out), .en_in(or_12_out));  // open: in6, in7, gs, en_out
  or or_12 (or_12_out, RType, IType, MemWrite, SBType, UType, UJType);
  Priority_Encoder #(.select(2), .disabled("Z")) priority_encoder_4 (
    .in1(and_10_out), .in2(comparator_20_eq), .out(priority_encoder_4_out), .en_in(or_11_out));  // open: in0, in3, gs, en_out
  // Probe on or_11_out
  Pull_Resistor #(.pull(0)) pull_resistor_3 (.node(priority_encoder_3_out));
  // Probe on AOP_I
  Multiplexer #(.select(2), .width(4), .disabled("Z"), .enable("false")) multiplexer_1 (
    .in0(rom_2_data), .in1(4'b0101), .in2(4'b0000), .out(AOP_I), .sel(priority_encoder_4_out));  // open: in3
  Pull_Resistor #(.pull(0)) pull_resistor_4 (.node(priority_encoder_4_out));
  // Probe on priority_encoder_3_out
  // Probe on priority_encoder_4_out
  Multiplexer #(.select(3), .width(4), .disabled("Z"), .enable("false")) multiplexer_2 (
    .in0(AOP_R), .in1(AOP_I), .in2(4'b0000), .in3(4'b0000), .in4(4'b1101), .in5(4'b0000), .out(ALUOP),
    .sel(priority_encoder_3_out));  // open: in6, in7
  // Probe on ALUOP

  // Other names for the same wires on the sheet: Funct7[6:0] = Instruction[31:25]; Funct3[2:0] = Instruction[14:12];
  //   AOP[3:0] = ALUOP; OPCODE[6:0] = Instruction[6:0]; SType = MemWrite

  // Notes on the sheet:
  //   Extract the filed in Instrutions
  //   contents of rom_1 (hex, n*v repeats v):
  //   0 a c 12*0 f 16*0 c 95*0 6 e 126*0 7 128*0 b 126*0 3 127*0 4 8 126*0 2 127*0 1 9
  //   contents of rom_2 (hex, n*v repeats v):
  //   0 6 7 7 3 4 2 1
endmodule

module AluModel (
  input  [31:0] A,
  input  [31:0] B,
  input  [3:0] ALUSel,
  output [31:0] Result
);

  wire adder_3_cout, bitselector_1_out, bitselector_2_out, xor_1_out;
  wire [0:0] slt_alu;
  wire [15:0] adder_5_out, undriven, undriven_2;
  wire [31:0] add, adder_1_out, adder_3_out, and_alu, divu_alu, mul_alu, mulh_alu, mulhu_alu,
       multiplexer_1_out, multiplexer_2_out, multiplier_1_cout, multiplier_1_out, negator_1_out,
       negator_2_out, not_1_out, not_2_out, or_alu, remu_alu, sll_alu, sra_alu, srl_alu, sub_alu, xor_alu;
  wire [31:16] vaddh_alu;

  BitSelector #(.width(32), .group(1)) bitselector_1 (.in(A), .out(bitselector_1_out), .sel({5{1'b1}}));
  BitSelector #(.width(32), .group(1)) bitselector_2 (.in(B), .out(bitselector_2_out), .sel({5{1'b1}}));
  Negator #(.width(32)) negator_1 (.in(A), .out(negator_1_out));
  Negator #(.width(32)) negator_2 (.in(B), .out(negator_2_out));
  Multiplexer #(.select(1), .width(32), .disabled("Z"), .enable("false")) multiplexer_1 (
    .in0(A), .in1(negator_1_out), .out(multiplexer_1_out), .sel(bitselector_1_out));
  Multiplexer #(.select(1), .width(32), .disabled("Z"), .enable("false")) multiplexer_2 (
    .in0(B), .in1(negator_2_out), .out(multiplexer_2_out), .sel(bitselector_2_out));
  Multiplier #(.width(32)) multiplier_1 (
    .a(multiplexer_1_out), .b(multiplexer_2_out), .out(multiplier_1_out), .cout(multiplier_1_cout));  // open: cin
  xor xor_1 (xor_1_out, bitselector_1_out, bitselector_2_out);
  assign not_1_out = ~multiplier_1_out;  // NOT_Gate not_1, 32 bits wide
  Adder #(.width(32)) adder_1 (.a({32{1'b0}}), .b(not_2_out), .out(adder_1_out), .cin(adder_3_cout));  // open: cout
  assign not_2_out = ~multiplier_1_cout;  // NOT_Gate not_2, 32 bits wide
  Adder #(.width(32)) adder_2 (.a(A), .b(B), .out(add));  // open: cin, cout
  assign and_alu = A & B;  // AND_Gate and_1, 32 bits wide
  assign or_alu = A | B;  // OR_Gate or_1, 32 bits wide
  assign xor_alu = A ^ B;  // XOR_Gate xor_2, 32 bits wide
  Shifter #(.width(32), .shift("lr")) shifter_1 (.in(A), .\dist (B[4:0]), .out(srl_alu));
  Shifter #(.width(32), .shift("ar")) shifter_2 (.in(A), .\dist (B[4:0]), .out(sra_alu));
  Shifter #(.width(32), .shift("ll")) shifter_3 (.in(A), .\dist (B[4:0]), .out(sll_alu));
  Comparator #(.width(32), .mode("twosComplement")) comparator_1 (.a(A), .b(B), .lt(slt_alu[0]));  // open: gt, eq
  Adder #(.width(32)) adder_3 (.a(32'h1), .b(not_1_out), .out(adder_3_out), .cout(adder_3_cout));  // open: cin
  Multiplexer #(.select(1), .width(32), .disabled("Z"), .enable("false")) multiplexer_3 (
    .in0(multiplier_1_out), .in1(adder_3_out), .out(mul_alu), .sel(xor_1_out));
  Multiplexer #(.select(1), .width(32), .disabled("Z"), .enable("false")) multiplexer_4 (
    .in0(multiplier_1_cout), .in1(adder_1_out), .out(mulh_alu), .sel(xor_1_out));
  Divider #(.width(32)) divider_1 (.a(A), .b(B), .out(divu_alu), .rem(remu_alu));  // open: upper
  Multiplier #(.width(32)) multiplier_2 (.a(A), .b(B), .cout(mulhu_alu));  // open: out, cin
  Subtractor #(.width(32)) subtractor_1 (.a(A), .b(B), .out(sub_alu));  // open: bin, bout
  // Probe on Result
  Multiplexer #(.select(4), .width(32), .disabled("Z"), .enable("false")) multiplexer_5 (
    .in0(add), .in1(and_alu), .in2(or_alu), .in3(xor_alu), .in4(srl_alu), .in5(sra_alu), .in6(sll_alu),
    .in7({{31{1'b0}}, slt_alu[0]}), .in8(divu_alu), .in9(remu_alu), .in10(mul_alu), .in11(mulhu_alu),
    .in12(sub_alu), .in13(B), .in14(mulh_alu), .in15({vaddh_alu, vaddh_alu}), .out(Result), .sel(ALUSel));
  Adder #(.width(16)) adder_4 (.a(A[31:16]), .b(B[31:16]), .out(vaddh_alu));  // open: cin, cout
  Adder #(.width(16)) adder_5 (.a(undriven), .b(undriven_2), .out(adder_5_out));  // open: cin, cout

  // Other names for the same wires on the sheet: vaddh_alu[15:0] = vaddh_alu

  // Notes on the sheet:
  //   INPUTS to your circuit
  //   DON'T CHANGE THE LOCATIONS OF THE INPUTS AND OUTPUTS!
  //   OUTPUT from your circuit
endmodule

module ImmModel (
  input  [31:0] INSTRUCTION,
  input  [2:0] InstructionType,
  output [31:0] Immdiate
);

  wire [31:0] bit_extender_1_out, bit_extender_2_out, bit_extender_3_out, bit_extender_4_out;

  // Probe on INSTRUCTION
  assign bit_extender_1_out = {{20{INSTRUCTION[31]}}, INSTRUCTION[31:20]};  // Bit_Extender bit_extender_1
  assign bit_extender_2_out = {{20{INSTRUCTION[31]}}, {INSTRUCTION[31:25], INSTRUCTION[11:7]}};  // Bit_Extender bit_extender_2
  assign bit_extender_3_out = {{19{INSTRUCTION[31]}}, {INSTRUCTION[31], INSTRUCTION[7], INSTRUCTION[30:25], INSTRUCTION[11:8], 1'b0}};  // Bit_Extender bit_extender_3
  // Probe on bit_extender_3_out
  assign bit_extender_4_out = {{11{INSTRUCTION[31]}}, {INSTRUCTION[31], INSTRUCTION[19:12], INSTRUCTION[20], INSTRUCTION[30:21], 1'b0}};  // Bit_Extender bit_extender_4
  Multiplexer #(.select(3), .width(32), .disabled("Z"), .enable("false")) multiplexer_1 (
    .in0(bit_extender_1_out), .in1(bit_extender_2_out), .in2(bit_extender_3_out),
    .in3({INSTRUCTION[31:12], {12{1'b0}}}), .in4(bit_extender_4_out), .out(Immdiate), .sel(InstructionType));  // open: in5, in6, in7

  // Notes on the sheet:
  //   I
  //   S
  //   U
  //   SB
  //   UJ
endmodule

module Branch (
  input  [31:0] RS1,
  input  [31:0] RS2,
  input  BrUN,
  output BrEQ,
  output BrLT
);

  wire comparator_1_lt, comparator_2_lt;

  Comparator #(.width(32), .mode("twosComplement")) comparator_1 (
    .a(RS1), .b(RS2), .eq(BrEQ), .lt(comparator_1_lt));  // open: gt
  Comparator #(.width(32), .mode("unsigned")) comparator_2 (.a(RS1), .b(RS2), .lt(comparator_2_lt));  // open: gt, eq
  Multiplexer #(.select(1), .width(1), .disabled("Z"), .enable("false")) multiplexer_1 (
    .in0(comparator_1_lt), .in1(comparator_2_lt), .out(BrLT), .sel(BrUN));
endmodule

module IMEM (
  input  [31:0] Program_counter,
  output [31:0] Instruction
);

  ROM #(.addrWidth(16), .dataWidth(32), .Select("high")) rom_1 (.addr(Program_counter[17:2]), .data(Instruction));

  // Notes on the sheet:
  //   contents of rom_1 (hex, n*v repeats v):
  //   fffff437 1234e493 12e293 1236313 1233e393 542023 642023 742023 449293 849313 c49393 542023 642023
  //   742023 1049293 1449313 13 542023 642023
endmodule

module DMEM (
  input  [31:0] Write_Data,
  input  clk,
  input  Read_En,
  input  [31:0] Address,
  input  Write_En,
  output [15:0] MissNubmer,
  output [31:0] Read_Data
);

  wire and_1_out, and_2_out, and_3_out, and_4_out, is_MemAddr, is_RomAddr, or_1_out;
  wire [15:0] controlled_buffer_3_out;
  wire [31:0] controlled_buffer_1_out, controlled_buffer_2_out, ram_1_data, rom_1_data;

  or or_1 (or_1_out, Read_En, Write_En);
  and and_1 (and_1_out, or_1_out, is_MemAddr);
  assign controlled_buffer_1_out = and_1_out ? Address : 32'bz;  // Controlled_Buffer controlled_buffer_1
  Comparator #(.width(4), .mode("unsigned")) comparator_1 (
    .a(Address[31:28]), .b(4'b1000), .eq(is_RomAddr));  // open: gt, lt
  assign controlled_buffer_2_out = and_2_out ? Write_Data : 32'bz;  // Controlled_Buffer controlled_buffer_2
  and and_2 (and_2_out, is_MemAddr, Write_En);
  assign controlled_buffer_3_out = is_RomAddr ? Address[17:2] : 16'bz;  // Controlled_Buffer controlled_buffer_3
  not not_1 (is_MemAddr, is_RomAddr);
  RAM #(.addrWidth(16), .dataWidth(32), .bus("separate"), .Select("high")) ram_1 (
    .addr(controlled_buffer_1_out[17:2]), .din(controlled_buffer_2_out), .data(ram_1_data), .str(and_2_out),
    .clk(clk), .ld(1'b1));  // open: sel, clr
  ROM #(.addrWidth(16), .dataWidth(32), .Select("high")) rom_1 (.addr(controlled_buffer_3_out), .data(rom_1_data));
  and and_3 (and_3_out, Read_En, is_MemAddr);
  assign Read_Data = and_3_out ? ram_1_data : 32'bz;  // Controlled_Buffer controlled_buffer_4
  assign Read_Data = and_4_out ? rom_1_data : 32'bz;  // Controlled_Buffer controlled_buffer_5
  and and_4 (and_4_out, Read_En, is_RomAddr);

  // Other names for the same wires on the sheet: Addr[31:0] = Address; MissNumber[15:0] = MissNubmer;
  //   ReadData[31:0] = Read_Data; ReadEnable = Read_En; WriteData[31:0] = Write_Data; WriteEnable = Write_En

  // Notes on the sheet:
  //   输入引脚区
  //   二级存储器
  //   contents of rom_1 (hex, n*v repeats v):
  //   0 1 2 3 4 5 6 7 8 9 a b c d e f 10 11 12 13 14 15 16 17 18 19 1a 1b 1c 1d 1e 1f 20 21 22 23 24 25 26
  //   27 28 29 2a 2b 2c 2d 2e 2f 30 31 32 33 34 35 36 37 38 39 3a 3b 3c 3d 3e 3f 40 41 42 43 44 45 46 47
  //   48 49 4a 4b 4c 4d 4e 4f 50 51 52 53 54 55 56 57 58 59 5a 5b 5c 5d 5e 5f 60 61 62 63 64 65 66 67 68
  //   69 6a 6b 6c 6d 6e 6f 70 71 72 73 74 75 76 77 78 79 7a 7b 7c 7d 7e 7f ffffff80 ffffff81 ffffff82
  //   ffffff83 ffffff84 ffffff85 ffffff86 ffffff87 ffffff88 ffffff89 ffffff8a ffffff8b ffffff8c ffffff8d
  //   ffffff8e ffffff8f ffffff90 ffffff91 ffffff92 ffffff93 ffffff94 ffffff95 ffffff96 ffffff97 ffffff98
  //   ffffff99 ffffff9a ffffff9b ffffff9c ffffff9d ffffff9e ffffff9f ffffffa0 ffffffa1 ffffffa2 ffffffa3
  //   ffffffa4 ffffffa5 ffffffa6 ffffffa7 ffffffa8 ffffffa9 ffffffaa ffffffab ffffffac ffffffad ffffffae
  //   ffffffaf ffffffb0 ffffffb1 ffffffb2 ffffffb3 ffffffb4 ffffffb5 ffffffb6 ffffffb7 ffffffb8 ffffffb9
  //   ffffffba ffffffbb ffffffbc ffffffbd ffffffbe ffffffbf ffffffc0 ffffffc1 ffffffc2 ffffffc3 ffffffc4
  //   ffffffc5 ffffffc6 ffffffc7 ffffffc8 ffffffc9 ffffffca ffffffcb ffffffcc ffffffcd ffffffce ffffffcf
  //   ffffffd0 ffffffd1 ffffffd2 ffffffd3 ffffffd4 ffffffd5 ffffffd6 ffffffd7 ffffffd8 ffffffd9 ffffffda
  //   ffffffdb ffffffdc ffffffdd ffffffde ffffffdf ffffffe0 ffffffe1 ffffffe2 ffffffe3 ffffffe4 ffffffe5
  //   ffffffe6 ffffffe7 ffffffe8 ffffffe9 ffffffea ffffffeb ffffffec ffffffed ffffffee ffffffef fffffff0
  //   fffffff1 fffffff2 fffffff3 fffffff4 fffffff5 fffffff6 fffffff7 fffffff8 fffffff9 fffffffa fffffffb
  //   fffffffc fffffffd fffffffe ffffffff 0 1 2 3 4 5 6 7 8 9 a b c d e f 10 11 12 13 14 15 16 17 18 19 1a
  //   1b 1c 1d 1e 1f 20 21 22 23 24 25 26 27 28 29 2a 2b 2c 2d 2e 2f 30 31 32 33 34 35 36 37 38 39 3a 3b
  //   3c 3d 3e 3f 40 41 42 43 44 45 46 47 48 49 4a 4b 4c 4d 4e 4f 50 51 52 53 54 55 56 57 58 59 5a 5b 5c
  //   5d 5e 5f 60 61 62 63 64 65 66 67 68 69 6a 6b 6c 6d 6e 6f 70 71 72 73 74 75 76 77 78 79 7a 7b 7c 7d
  //   7e 7f ffffff80 ffffff81 ffffff82 ffffff83 ffffff84 ffffff85 ffffff86 ffffff87 ffffff88 ffffff89
  //   ffffff8a ffffff8b ffffff8c ffffff8d ffffff8e ffffff8f ffffff90 ffffff91 ffffff92 ffffff93 ffffff94
  //   ffffff95 ffffff96 ffffff97 ffffff98 ffffff99 ffffff9a ffffff9b ffffff9c ffffff9d ffffff9e ffffff9f
  //   ffffffa0 ffffffa1 ffffffa2 ffffffa3 ffffffa4 ffffffa5 ffffffa6 ffffffa7 ffffffa8 ffffffa9 ffffffaa
  //   ffffffab ffffffac ffffffad ffffffae ffffffaf ffffffb0 ffffffb1 ffffffb2 ffffffb3 ffffffb4 ffffffb5
  //   ffffffb6 ffffffb7 ffffffb8 ffffffb9 ffffffba ffffffbb ffffffbc ffffffbd ffffffbe ffffffbf ffffffc0
  //   ffffffc1 ffffffc2 ffffffc3 ffffffc4 ffffffc5 ffffffc6 ffffffc7 ffffffc8 ffffffc9 ffffffca ffffffcb
  //   ffffffcc ffffffcd ffffffce ffffffcf ffffffd0 ffffffd1 ffffffd2 ffffffd3 ffffffd4 ffffffd5 ffffffd6
  //   ffffffd7 ffffffd8 ffffffd9 ffffffda ffffffdb ffffffdc ffffffdd ffffffde ffffffdf ffffffe0 ffffffe1
  //   ffffffe2 ffffffe3 ffffffe4 ffffffe5 ffffffe6 ffffffe7 ffffffe8 ffffffe9 ffffffea ffffffeb ffffffec
  //   ffffffed ffffffee ffffffef fffffff0 fffffff1 fffffff2 fffffff3 fffffff4 fffffff5 fffffff6 fffffff7
  //   fffffff8 fffffff9 fffffffa fffffffb fffffffc fffffffd fffffffe ffffffff 0 1 2 3 4 5 6 7 8 9 a b c d
  //   e f 10 11 12 13 14 15 16 17 18 19 1a 1b 1c 1d 1e 1f 20 21 22 23 24 25 26 27 28 29 2a 2b 2c 2d 2e 2f
  //   30 31 32 33 34 35 36 37 38 39 3a 3b 3c 3d 3e 3f 40 41 42 43 44 45 46 47 48 49 4a 4b 4c 4d 4e 4f 50
  //   51 52 53 54 55 56 57 58 59 5a 5b 5c 5d 5e 5f 60 61 62 63 64 65 66 67 68 69 6a 6b 6c 6d 6e 6f 70 71
  //   72 73 74 75 76 77 78 79 7a 7b 7c 7d 7e 7f ffffff80 ffffff81 ffffff82 ffffff83 ffffff84 ffffff85
  //   ffffff86 ffffff87 ffffff88 ffffff89 ffffff8a ffffff8b ffffff8c ffffff8d ffffff8e ffffff8f ffffff90
  //   ffffff91 ffffff92 ffffff93 ffffff94 ffffff95 ffffff96 ffffff97 ffffff98 ffffff99 ffffff9a ffffff9b
  //   ffffff9c ffffff9d ffffff9e ffffff9f ffffffa0 ffffffa1 ffffffa2 ffffffa3 ffffffa4 ffffffa5 ffffffa6
  //   ffffffa7 ffffffa8 ffffffa9 ffffffaa ffffffab ffffffac ffffffad ffffffae ffffffaf ffffffb0 ffffffb1
  //   ffffffb2 ffffffb3 ffffffb4 ffffffb5 ffffffb6 ffffffb7 ffffffb8 ffffffb9 ffffffba ffffffbb ffffffbc
  //   ffffffbd ffffffbe ffffffbf ffffffc0 ffffffc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
  //   输出引脚区
endmodule

module BusModel (
  input  [31:0] WriteAddr,
  input  [31:0] WriteData,
  input  R,
  input  W,
  input  [31:0] IORead,
  input  [31:0] MemRead,
  output [31:0] ReadData,
  output out_8,
  output IOEn,
  output [11:0] IOAddr12,
  output [31:0] IOWriteData,
  output [31:0] MemAddr,
  output MemR,
  output MemW,
  output [31:0] MemWriteData
);

  wire and_1_out, and_2_out, and_3_out, and_4_out, is_MemAddr, or_1_out;

  // Probe on WriteAddr
  assign MemW = is_MemAddr ? W : 1'bz;  // Controlled_Buffer controlled_buffer_1
  Comparator #(.width(20), .mode("unsigned")) comparator_1 (
    .a(WriteAddr[31:12]), .b({20{1'b1}}), .eq(IOEn));  // open: gt, lt
  assign MemR = is_MemAddr ? R : 1'bz;  // Controlled_Buffer controlled_buffer_2
  // Probe on IOEn
  not not_1 (is_MemAddr, IOEn);
  or or_1 (or_1_out, R, W);
  and and_1 (and_1_out, is_MemAddr, or_1_out);
  // Probe on WriteAddr
  assign MemAddr = and_1_out ? WriteAddr : 32'bz;  // Controlled_Buffer controlled_buffer_3
  // Probe on MemAddr
  and and_2 (and_2_out, is_MemAddr, W);
  assign MemWriteData = and_2_out ? WriteData : 32'bz;  // Controlled_Buffer controlled_buffer_4
  and and_3 (and_3_out, R, IOEn);
  assign ReadData = and_3_out ? IORead : 32'bz;  // Controlled_Buffer controlled_buffer_5
  assign ReadData = and_4_out ? MemRead : 32'bz;  // Controlled_Buffer controlled_buffer_6
  and and_4 (and_4_out, R, is_MemAddr);
  // Probe on ReadData

  assign IOAddr12 = WriteAddr[11:0];
  assign IOWriteData = WriteData;

  // Other names for the same wires on the sheet: IORW = out_8; RW = out_8
endmodule

module LedDriver (
  input  IOEn,
  input  [11:0] IOAddr12,
  input  [31:0] IOWriteData,
  input  in_4,
  output [31:0] DisplayData
);

  wire and_1_out, comparator_1_eq;
  wire [31:0] multiplexer_1_out;

  Comparator #(.width(12), .mode("unsigned")) comparator_1 (
    .a({12{1'b0}}), .b(IOAddr12), .eq(comparator_1_eq));  // open: gt, lt
  and and_1 (and_1_out, comparator_1_eq, IOEn);
  Multiplexer #(.select(1), .width(32), .disabled("Z"), .enable("false")) multiplexer_1 (
    .in1(IOWriteData), .out(multiplexer_1_out), .sel(and_1_out));  // open: in0
  Register #(.width(32), .trigger("rising"), .Select("low")) register_1 (
    .D(multiplexer_1_out), .en(and_1_out), .Q(DisplayData), .clk(in_4));  // open: clr

  // Other names for the same wires on the sheet: clk = in_4
endmodule

module KeyTTYDriver (
  input  IOEn,
  input  in_2,
  input  [11:0] IOAddr12,
  input  [31:0] IOWriteData,
  input  clk,
  input  [6:0] KeyValue,
  input  KeyEn,
  output clock,
  output [31:0] IORead,
  output [6:0] TTYData,
  output TTYEnable
);

  wire and_1_out, comparator_1_eq, comparator_2_eq;

  Comparator #(.width(12), .mode("unsigned")) comparator_1 (
    .a(12'h4), .b(IOAddr12), .eq(comparator_1_eq));  // open: gt, lt
  Comparator #(.width(12), .mode("unsigned")) comparator_2 (
    .a(12'h8), .b(IOAddr12), .eq(comparator_2_eq));  // open: gt, lt
  and and_1 (and_1_out, comparator_1_eq, IOEn);
  and and_2 (TTYEnable, comparator_2_eq, IOEn);
  // Probe on IOEn
  // Probe on IOWriteData
  Multiplexer #(.select(1), .width(32), .disabled("Z"), .enable("false")) multiplexer_1 (
    .in1({KeyEn, {24{1'b0}}, KeyValue}), .out(IORead), .sel(and_1_out));  // open: in0
  Multiplexer #(.select(1), .width(7), .disabled("Z"), .enable("false")) multiplexer_2 (
    .in1(IOWriteData[6:0]), .out(TTYData), .sel(TTYEnable));  // open: in0
  // Probe on IORead

  assign clock = clk;

  // Other names for the same wires on the sheet: IORW = in_2
endmodule

module DMEMCache (
  input  [31:0] Write_Data,
  input  clk,
  input  Read_En,
  input  [31:0] Address,
  input  Write_En,
  output Miss,
  output [15:0] MissNubmer,
  output [31:0] Read_Data
);

  wire and_1_out, and_2_out, and_3_out, and_4_out, and_5_out, \cache直接相联_1_miss , is_MemAddr, is_RomAddr,
       or_1_out, RDY;
  wire [15:0] controlled_buffer_4_out, controlled_buffer_6_out, counter_1_q, ExChangeAddr;
  wire [31:0] \cache直接相联_1_dataout , controlled_buffer_1_out, controlled_buffer_5_out,
       exchange_logic_1_blockdatain0, exchange_logic_1_blockdatain1, exchange_logic_1_blockdatain2,
       exchange_logic_1_blockdatain3, ExChangeData, RAM_data, rom_1_data;

  assign controlled_buffer_1_out = Read_En ? Address : 32'bz;  // Controlled_Buffer controlled_buffer_1
  Pull_Resistor #(.pull(0)) pull_resistor_1 (.node(controlled_buffer_1_out));
  Comparator #(.width(4), .mode("unsigned")) comparator_1 (
    .a(Address[31:28]), .b(4'b1000), .eq(is_RomAddr));  // open: gt, lt
  not not_1 (is_MemAddr, is_RomAddr);
  assign Read_Data = Read_En ? \cache直接相联_1_dataout  : 32'bz;  // Controlled_Buffer controlled_buffer_2
  \Cache直接相联  \cache直接相联_1  (
    .BlockDataIn(exchange_logic_1_blockdatain0), .Addr(controlled_buffer_1_out[17:2]), .BlkDataReady(RDY),
    .CLK(clk), .Miss(\cache直接相联_1_miss ), .DataOut(\cache直接相联_1_dataout ),
    .BlockDataIn_2(exchange_logic_1_blockdatain1), .BlockDataIn_3(exchange_logic_1_blockdatain2),
    .BlockDataIn_4(exchange_logic_1_blockdatain3));
  assign Miss = Read_En ? \cache直接相联_1_miss  : 1'bz;  // Controlled_Buffer controlled_buffer_3
  Pull_Resistor #(.pull(0)) pull_resistor_2 (.node(Miss));
  or or_1 (or_1_out, Read_En, Write_En);
  ExChange_logic exchange_logic_1 (
    .Addr(controlled_buffer_1_out[17:2]), .ByteDataIn(ExChangeData), .Miss(\cache直接相联_1_miss ),
    .Enable(Read_En), .CLK(clk), .ByteAddrOut(ExChangeAddr), .BlockDataIn0(exchange_logic_1_blockdatain0),
    .BlkDataReady(RDY), .BlockDataIn1(exchange_logic_1_blockdatain1),
    .BlockDataIn2(exchange_logic_1_blockdatain2), .BlockDataIn3(exchange_logic_1_blockdatain3));
  and and_1 (and_1_out, or_1_out, is_MemAddr);
  assign controlled_buffer_4_out = and_1_out ? Address[17:2] : 16'bz;  // Controlled_Buffer controlled_buffer_4
  and and_2 (and_2_out, Miss, RDY);
  Counter #(.width(16), .max('hffff), .ongoal("wrap"), .trigger("rising"), .behavior("old")) counter_1 (
    .count(and_2_out), .Q(counter_1_q), .clk(clk));  // open: load, D, carry, clr, preset
  and and_3 (and_3_out, is_MemAddr, Write_En);
  Register #(.width(16), .trigger("rising"), .Select("low")) register_1 (
    .D(counter_1_q), .Q(MissNubmer), .clk(clk));  // open: en, clr
  assign controlled_buffer_5_out = and_3_out ? Write_Data : 32'bz;  // Controlled_Buffer controlled_buffer_5
  assign controlled_buffer_6_out = is_RomAddr ? ExChangeAddr : 16'bz;  // Controlled_Buffer controlled_buffer_6
  RAM #(.addrWidth(16), .dataWidth(32), .bus("separate"), .Select("high")) RAM (
    .addr(controlled_buffer_4_out), .din(controlled_buffer_5_out), .data(RAM_data), .str(and_3_out),
    .clk(clk), .ld(1'b1));  // open: sel, clr
  ROM #(.addrWidth(16), .dataWidth(32), .Select("high")) rom_1 (.addr(controlled_buffer_6_out), .data(rom_1_data));
  and and_4 (and_4_out, Read_En, is_MemAddr);
  assign ExChangeData = and_4_out ? RAM_data : 32'bz;  // Controlled_Buffer controlled_buffer_7
  assign ExChangeData = and_5_out ? rom_1_data : 32'bz;  // Controlled_Buffer controlled_buffer_8
  and and_5 (and_5_out, Read_En, is_RomAddr);

  // Other names for the same wires on the sheet: Addr[31:0] = Address; MissNumber[15:0] = MissNubmer;
  //   ReadData[31:0] = Read_Data; ReadEnable = Read_En; WriteData[31:0] = Write_Data; WriteEnable = Write_En

  // Notes on the sheet:
  //   输入引脚区
  //   输出引脚区
  //   二级存储器
  //   高电平为Miss
  //   contents of rom_1 (hex, n*v repeats v):
  //   0 1 2 3 4 5 6 7 8 9 a b c d e f 10 11 12 13 14 15 16 17 18 19 1a 1b 1c 1d 1e 1f 20 21 22 23 24 25 26
  //   27 28 29 2a 2b 2c 2d 2e 2f 30 31 32 33 34 35 36 37 38 39 3a 3b 3c 3d 3e 3f 40 41 42 43 44 45 46 47
  //   48 49 4a 4b 4c 4d 4e 4f 50 51 52 53 54 55 56 57 58 59 5a 5b 5c 5d 5e 5f 60 61 62 63 64 65 66 67 68
  //   69 6a 6b 6c 6d 6e 6f 70 71 72 73 74 75 76 77 78 79 7a 7b 7c 7d 7e 7f ffffff80 ffffff81 ffffff82
  //   ffffff83 ffffff84 ffffff85 ffffff86 ffffff87 ffffff88 ffffff89 ffffff8a ffffff8b ffffff8c ffffff8d
  //   ffffff8e ffffff8f ffffff90 ffffff91 ffffff92 ffffff93 ffffff94 ffffff95 ffffff96 ffffff97 ffffff98
  //   ffffff99 ffffff9a ffffff9b ffffff9c ffffff9d ffffff9e ffffff9f ffffffa0 ffffffa1 ffffffa2 ffffffa3
  //   ffffffa4 ffffffa5 ffffffa6 ffffffa7 ffffffa8 ffffffa9 ffffffaa ffffffab ffffffac ffffffad ffffffae
  //   ffffffaf ffffffb0 ffffffb1 ffffffb2 ffffffb3 ffffffb4 ffffffb5 ffffffb6 ffffffb7 ffffffb8 ffffffb9
  //   ffffffba ffffffbb ffffffbc ffffffbd ffffffbe ffffffbf ffffffc0 ffffffc1 ffffffc2 ffffffc3 ffffffc4
  //   ffffffc5 ffffffc6 ffffffc7 ffffffc8 ffffffc9 ffffffca ffffffcb ffffffcc ffffffcd ffffffce ffffffcf
  //   ffffffd0 ffffffd1 ffffffd2 ffffffd3 ffffffd4 ffffffd5 ffffffd6 ffffffd7 ffffffd8 ffffffd9 ffffffda
  //   ffffffdb ffffffdc ffffffdd ffffffde ffffffdf ffffffe0 ffffffe1 ffffffe2 ffffffe3 ffffffe4 ffffffe5
  //   ffffffe6 ffffffe7 ffffffe8 ffffffe9 ffffffea ffffffeb ffffffec ffffffed ffffffee ffffffef fffffff0
  //   fffffff1 fffffff2 fffffff3 fffffff4 fffffff5 fffffff6 fffffff7 fffffff8 fffffff9 fffffffa fffffffb
  //   fffffffc fffffffd fffffffe ffffffff 0 1 2 3 4 5 6 7 8 9 a b c d e f 10 11 12 13 14 15 16 17 18 19 1a
  //   1b 1c 1d 1e 1f 20 21 22 23 24 25 26 27 28 29 2a 2b 2c 2d 2e 2f 30 31 32 33 34 35 36 37 38 39 3a 3b
  //   3c 3d 3e 3f 40 41 42 43 44 45 46 47 48 49 4a 4b 4c 4d 4e 4f 50 51 52 53 54 55 56 57 58 59 5a 5b 5c
  //   5d 5e 5f 60 61 62 63 64 65 66 67 68 69 6a 6b 6c 6d 6e 6f 70 71 72 73 74 75 76 77 78 79 7a 7b 7c 7d
  //   7e 7f ffffff80 ffffff81 ffffff82 ffffff83 ffffff84 ffffff85 ffffff86 ffffff87 ffffff88 ffffff89
  //   ffffff8a ffffff8b ffffff8c ffffff8d ffffff8e ffffff8f ffffff90 ffffff91 ffffff92 ffffff93 ffffff94
  //   ffffff95 ffffff96 ffffff97 ffffff98 ffffff99 ffffff9a ffffff9b ffffff9c ffffff9d ffffff9e ffffff9f
  //   ffffffa0 ffffffa1 ffffffa2 ffffffa3 ffffffa4 ffffffa5 ffffffa6 ffffffa7 ffffffa8 ffffffa9 ffffffaa
  //   ffffffab ffffffac ffffffad ffffffae ffffffaf ffffffb0 ffffffb1 ffffffb2 ffffffb3 ffffffb4 ffffffb5
  //   ffffffb6 ffffffb7 ffffffb8 ffffffb9 ffffffba ffffffbb ffffffbc ffffffbd ffffffbe ffffffbf ffffffc0
  //   ffffffc1 ffffffc2 ffffffc3 ffffffc4 ffffffc5 ffffffc6 ffffffc7 ffffffc8 ffffffc9 ffffffca ffffffcb
  //   ffffffcc ffffffcd ffffffce ffffffcf ffffffd0 ffffffd1 ffffffd2 ffffffd3 ffffffd4 ffffffd5 ffffffd6
  //   ffffffd7 ffffffd8 ffffffd9 ffffffda ffffffdb ffffffdc ffffffdd ffffffde ffffffdf ffffffe0 ffffffe1
  //   ffffffe2 ffffffe3 ffffffe4 ffffffe5 ffffffe6 ffffffe7 ffffffe8 ffffffe9 ffffffea ffffffeb ffffffec
  //   ffffffed ffffffee ffffffef fffffff0 fffffff1 fffffff2 fffffff3 fffffff4 fffffff5 fffffff6 fffffff7
  //   fffffff8 fffffff9 fffffffa fffffffb fffffffc fffffffd fffffffe ffffffff 0 1 2 3 4 5 6 7 8 9 a b c d
  //   e f 10 11 12 13 14 15 16 17 18 19 1a 1b 1c 1d 1e 1f 20 21 22 23 24 25 26 27 28 29 2a 2b 2c 2d 2e 2f
  //   30 31 32 33 34 35 36 37 38 39 3a 3b 3c 3d 3e 3f 40 41 42 43 44 45 46 47 48 49 4a 4b 4c 4d 4e 4f 50
  //   51 52 53 54 55 56 57 58 59 5a 5b 5c 5d 5e 5f 60 61 62 63 64 65 66 67 68 69 6a 6b 6c 6d 6e 6f 70 71
  //   72 73 74 75 76 77 78 79 7a 7b 7c 7d 7e 7f ffffff80 ffffff81 ffffff82 ffffff83 ffffff84 ffffff85
  //   ffffff86 ffffff87 ffffff88 ffffff89 ffffff8a ffffff8b ffffff8c ffffff8d ffffff8e ffffff8f ffffff90
  //   ffffff91 ffffff92 ffffff93 ffffff94 ffffff95 ffffff96 ffffff97 ffffff98 ffffff99 ffffff9a ffffff9b
  //   ffffff9c ffffff9d ffffff9e ffffff9f ffffffa0 ffffffa1 ffffffa2 ffffffa3 ffffffa4 ffffffa5 ffffffa6
  //   ffffffa7 ffffffa8 ffffffa9 ffffffaa ffffffab ffffffac ffffffad ffffffae ffffffaf ffffffb0 ffffffb1
  //   ffffffb2 ffffffb3 ffffffb4 ffffffb5 ffffffb6 ffffffb7 ffffffb8 ffffffb9 ffffffba ffffffbb ffffffbc
  //   ffffffbd ffffffbe ffffffbf ffffffc0 ffffffc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
endmodule

module \Cache直接相联  (
  input  [31:0] BlockDataIn,
  input  [31:0] BlockDataIn_2,
  input  [31:0] BlockDataIn_3,
  input  [31:0] BlockDataIn_4,
  input  [15:0] Addr,
  input  BlkDataReady,
  input  CLK,
  output Miss,
  output [31:0] DataOut
);

  wire and_1_out, and_2_out, and_3_out, and_4_out, and_5_out, and_6_out, and_7_out, and_8_out,
       comparator_1_eq, L0, L1, L2, L3, L4, L5, L6, L7, Valid, VALID_2_q, VALID_3_q, VALID_4_q, VALID_5_q,
       VALID_6_q, VALID_7_q, VALID_8_q, VALID_q;
  wire [10:0] TAG_2_q, TAG_3_q, TAG_4_q, TAG_5_q, TAG_6_q, TAG_7_q, TAG_8_q, TAG_q, TagData;
  wire [31:0] SlotData0, SlotData1, SlotData2, SlotData3, \数据块副本_2_q , \数据块副本_3_q , \数据块副本_4_q , \数据块副本_5_q ,
       \数据块副本_6_q , \数据块副本_7_q , \数据块副本_8_q , \数据块副本_9_q , \数据块副本_10_q , \数据块副本_11_q , \数据块副本_12_q ,
       \数据块副本_13_q , \数据块副本_14_q , \数据块副本_15_q , \数据块副本_16_q , \数据块副本_17_q , \数据块副本_18_q , \数据块副本_19_q ,
       \数据块副本_20_q , \数据块副本_21_q , \数据块副本_22_q , \数据块副本_23_q , \数据块副本_24_q , \数据块副本_25_q , \数据块副本_26_q ,
       \数据块副本_27_q , \数据块副本_28_q , \数据块副本_29_q , \数据块副本_30_q , \数据块副本_31_q , \数据块副本_32_q , \数据块副本_q ;

  Register #(.width(1), .trigger("rising"), .Select("low")) u_VALID (
    .D(1'b1), .en(and_1_out), .Q(VALID_q), .clk(CLK));  // open: clr
  assign Valid = L0 ? VALID_q : 1'bz;  // Controlled_Buffer controlled_buffer_1
  Register #(.width(1), .trigger("rising"), .Select("low")) VALID_2 (
    .D(1'b1), .en(and_2_out), .Q(VALID_2_q), .clk(CLK));  // open: clr
  assign Valid = L1 ? VALID_2_q : 1'bz;  // Controlled_Buffer controlled_buffer_2
  assign Valid = L2 ? VALID_3_q : 1'bz;  // Controlled_Buffer controlled_buffer_3
  Register #(.width(1), .trigger("rising"), .Select("low")) VALID_3 (
    .D(1'b1), .en(and_3_out), .Q(VALID_3_q), .clk(CLK));  // open: clr
  Register #(.width(1), .trigger("rising"), .Select("low")) VALID_4 (
    .D(1'b1), .en(and_4_out), .Q(VALID_4_q), .clk(CLK));  // open: clr
  assign Valid = L3 ? VALID_4_q : 1'bz;  // Controlled_Buffer controlled_buffer_4
  assign Valid = L4 ? VALID_5_q : 1'bz;  // Controlled_Buffer controlled_buffer_5
  Register #(.width(1), .trigger("rising"), .Select("low")) VALID_5 (
    .D(1'b1), .en(and_5_out), .Q(VALID_5_q), .clk(CLK));  // open: clr
  Register #(.width(1), .trigger("rising"), .Select("low")) VALID_6 (
    .D(1'b1), .en(and_6_out), .Q(VALID_6_q), .clk(CLK));  // open: clr
  assign Valid = L5 ? VALID_6_q : 1'bz;  // Controlled_Buffer controlled_buffer_6
  assign Valid = L6 ? VALID_7_q : 1'bz;  // Controlled_Buffer controlled_buffer_7
  Register #(.width(1), .trigger("rising"), .Select("low")) VALID_7 (
    .D(1'b1), .en(and_7_out), .Q(VALID_7_q), .clk(CLK));  // open: clr
  Register #(.width(1), .trigger("rising"), .Select("low")) VALID_8 (
    .D(1'b1), .en(and_8_out), .Q(VALID_8_q), .clk(CLK));  // open: clr
  assign Valid = L7 ? VALID_8_q : 1'bz;  // Controlled_Buffer controlled_buffer_8
  Decoder #(.select(3), .tristate("false"), .disabled("Z"), .enable("false")) decoder_1 (
    .out0(L0), .out1(L1), .out2(L2), .out3(L3), .out4(L4), .out5(L5), .out6(L6), .out7(L7), .sel(Addr[4:2]));
  Register #(.width(11), .trigger("rising"), .Select("low")) TAG (
    .D(Addr[15:5]), .en(and_1_out), .Q(TAG_q), .clk(CLK));  // open: clr
  Register #(.width(11), .trigger("rising"), .Select("low")) TAG_2 (
    .D(Addr[15:5]), .en(and_2_out), .Q(TAG_2_q), .clk(CLK));  // open: clr
  Register #(.width(11), .trigger("rising"), .Select("low")) TAG_3 (
    .D(Addr[15:5]), .en(and_3_out), .Q(TAG_3_q), .clk(CLK));  // open: clr
  Register #(.width(11), .trigger("rising"), .Select("low")) TAG_4 (
    .D(Addr[15:5]), .en(and_4_out), .Q(TAG_4_q), .clk(CLK));  // open: clr
  Register #(.width(11), .trigger("rising"), .Select("low")) TAG_5 (
    .D(Addr[15:5]), .en(and_5_out), .Q(TAG_5_q), .clk(CLK));  // open: clr
  Register #(.width(11), .trigger("rising"), .Select("low")) TAG_6 (
    .D(Addr[15:5]), .en(and_6_out), .Q(TAG_6_q), .clk(CLK));  // open: clr
  Register #(.width(11), .trigger("rising"), .Select("low")) TAG_7 (
    .D(Addr[15:5]), .en(and_7_out), .Q(TAG_7_q), .clk(CLK));  // open: clr
  assign TagData = L0 ? TAG_q : 11'bz;  // Controlled_Buffer controlled_buffer_9
  assign TagData = L1 ? TAG_2_q : 11'bz;  // Controlled_Buffer controlled_buffer_10
  assign TagData = L2 ? TAG_3_q : 11'bz;  // Controlled_Buffer controlled_buffer_11
  assign TagData = L3 ? TAG_4_q : 11'bz;  // Controlled_Buffer controlled_buffer_12
  assign TagData = L4 ? TAG_5_q : 11'bz;  // Controlled_Buffer controlled_buffer_13
  assign TagData = L5 ? TAG_6_q : 11'bz;  // Controlled_Buffer controlled_buffer_14
  assign TagData = L6 ? TAG_7_q : 11'bz;  // Controlled_Buffer controlled_buffer_15
  assign TagData = L7 ? TAG_8_q : 11'bz;  // Controlled_Buffer controlled_buffer_16
  Register #(.width(11), .trigger("rising"), .Select("low")) TAG_8 (
    .D(Addr[15:5]), .en(and_8_out), .Q(TAG_8_q), .clk(CLK));  // open: clr
  Comparator #(.width(11), .mode("twosComplement")) comparator_1 (
    .a(Addr[15:5]), .b(TagData), .eq(comparator_1_eq));  // open: gt, lt
  Register #(.width(32), .trigger("rising"), .Select("low")) \u_数据块副本  (
    .D(BlockDataIn), .en(and_1_out), .Q(\数据块副本_q ), .clk(CLK));  // open: clr
  Register #(.width(32), .trigger("rising"), .Select("low")) \u_数据块副本_2  (
    .D(BlockDataIn), .en(and_2_out), .Q(\数据块副本_2_q ), .clk(CLK));  // open: clr
  Register #(.width(32), .trigger("rising"), .Select("low")) \u_数据块副本_3  (
    .D(BlockDataIn), .en(and_3_out), .Q(\数据块副本_3_q ), .clk(CLK));  // open: clr
  Register #(.width(32), .trigger("rising"), .Select("low")) \u_数据块副本_4  (
    .D(BlockDataIn), .en(and_4_out), .Q(\数据块副本_4_q ), .clk(CLK));  // open: clr
  Register #(.width(32), .trigger("rising"), .Select("low")) \u_数据块副本_5  (
    .D(BlockDataIn), .en(and_5_out), .Q(\数据块副本_5_q ), .clk(CLK));  // open: clr
  Register #(.width(32), .trigger("rising"), .Select("low")) \u_数据块副本_6  (
    .D(BlockDataIn), .en(and_6_out), .Q(\数据块副本_6_q ), .clk(CLK));  // open: clr
  Register #(.width(32), .trigger("rising"), .Select("low")) \u_数据块副本_7  (
    .D(BlockDataIn), .en(and_7_out), .Q(\数据块副本_7_q ), .clk(CLK));  // open: clr
  Register #(.width(32), .trigger("rising"), .Select("low")) \u_数据块副本_8  (
    .D(BlockDataIn), .en(and_8_out), .Q(\数据块副本_8_q ), .clk(CLK));  // open: clr
  assign SlotData0 = L0 ? \数据块副本_q  : 32'bz;  // Controlled_Buffer controlled_buffer_17
  assign SlotData0 = L1 ? \数据块副本_2_q  : 32'bz;  // Controlled_Buffer controlled_buffer_18
  assign SlotData0 = L2 ? \数据块副本_3_q  : 32'bz;  // Controlled_Buffer controlled_buffer_19
  assign SlotData0 = L3 ? \数据块副本_4_q  : 32'bz;  // Controlled_Buffer controlled_buffer_20
  assign SlotData0 = L4 ? \数据块副本_5_q  : 32'bz;  // Controlled_Buffer controlled_buffer_21
  assign SlotData0 = L5 ? \数据块副本_6_q  : 32'bz;  // Controlled_Buffer controlled_buffer_22
  assign SlotData0 = L6 ? \数据块副本_7_q  : 32'bz;  // Controlled_Buffer controlled_buffer_23
  assign SlotData0 = L7 ? \数据块副本_8_q  : 32'bz;  // Controlled_Buffer controlled_buffer_24
  nand nand_1 (Miss, comparator_1_eq, Valid);
  Multiplexer #(.select(2), .width(32), .disabled("Z"), .enable("false")) multiplexer_1 (
    .in0(SlotData0), .in1(SlotData1), .in2(SlotData2), .in3(SlotData3), .out(DataOut), .sel(Addr[1:0]));
  Register #(.width(32), .trigger("rising"), .Select("low")) \u_数据块副本_9  (
    .D(BlockDataIn_2), .en(and_1_out), .Q(\数据块副本_9_q ), .clk(CLK));  // open: clr
  assign SlotData1 = L0 ? \数据块副本_9_q  : 32'bz;  // Controlled_Buffer controlled_buffer_25
  Register #(.width(32), .trigger("rising"), .Select("low")) \u_数据块副本_10  (
    .D(BlockDataIn_2), .en(and_2_out), .Q(\数据块副本_10_q ), .clk(CLK));  // open: clr
  assign SlotData1 = L1 ? \数据块副本_10_q  : 32'bz;  // Controlled_Buffer controlled_buffer_26
  Register #(.width(32), .trigger("rising"), .Select("low")) \u_数据块副本_11  (
    .D(BlockDataIn_2), .en(and_3_out), .Q(\数据块副本_11_q ), .clk(CLK));  // open: clr
  assign SlotData1 = L2 ? \数据块副本_11_q  : 32'bz;  // Controlled_Buffer controlled_buffer_27
  Register #(.width(32), .trigger("rising"), .Select("low")) \u_数据块副本_12  (
    .D(BlockDataIn_2), .en(and_4_out), .Q(\数据块副本_12_q ), .clk(CLK));  // open: clr
  assign SlotData1 = L3 ? \数据块副本_12_q  : 32'bz;  // Controlled_Buffer controlled_buffer_28
  Register #(.width(32), .trigger("rising"), .Select("low")) \u_数据块副本_13  (
    .D(BlockDataIn_2), .en(and_5_out), .Q(\数据块副本_13_q ), .clk(CLK));  // open: clr
  assign SlotData1 = L4 ? \数据块副本_13_q  : 32'bz;  // Controlled_Buffer controlled_buffer_29
  assign SlotData1 = L5 ? \数据块副本_14_q  : 32'bz;  // Controlled_Buffer controlled_buffer_30
  Register #(.width(32), .trigger("rising"), .Select("low")) \u_数据块副本_14  (
    .D(BlockDataIn_2), .en(and_6_out), .Q(\数据块副本_14_q ), .clk(CLK));  // open: clr
  Register #(.width(32), .trigger("rising"), .Select("low")) \u_数据块副本_15  (
    .D(BlockDataIn_2), .en(and_7_out), .Q(\数据块副本_15_q ), .clk(CLK));  // open: clr
  assign SlotData1 = L6 ? \数据块副本_15_q  : 32'bz;  // Controlled_Buffer controlled_buffer_31
  Register #(.width(32), .trigger("rising"), .Select("low")) \u_数据块副本_16  (
    .D(BlockDataIn_2), .en(and_8_out), .Q(\数据块副本_16_q ), .clk(CLK));  // open: clr
  assign SlotData1 = L7 ? \数据块副本_16_q  : 32'bz;  // Controlled_Buffer controlled_buffer_32
  Register #(.width(32), .trigger("rising"), .Select("low")) \u_数据块副本_17  (
    .D(BlockDataIn_3), .en(and_1_out), .Q(\数据块副本_17_q ), .clk(CLK));  // open: clr
  assign SlotData2 = L0 ? \数据块副本_17_q  : 32'bz;  // Controlled_Buffer controlled_buffer_33
  Register #(.width(32), .trigger("rising"), .Select("low")) \u_数据块副本_18  (
    .D(BlockDataIn_3), .en(and_2_out), .Q(\数据块副本_18_q ), .clk(CLK));  // open: clr
  assign SlotData2 = L1 ? \数据块副本_18_q  : 32'bz;  // Controlled_Buffer controlled_buffer_34
  assign SlotData2 = L2 ? \数据块副本_19_q  : 32'bz;  // Controlled_Buffer controlled_buffer_35
  Register #(.width(32), .trigger("rising"), .Select("low")) \u_数据块副本_19  (
    .D(BlockDataIn_3), .en(and_3_out), .Q(\数据块副本_19_q ), .clk(CLK));  // open: clr
  assign SlotData2 = L3 ? \数据块副本_20_q  : 32'bz;  // Controlled_Buffer controlled_buffer_36
  Register #(.width(32), .trigger("rising"), .Select("low")) \u_数据块副本_20  (
    .D(BlockDataIn_3), .en(and_4_out), .Q(\数据块副本_20_q ), .clk(CLK));  // open: clr
  Register #(.width(32), .trigger("rising"), .Select("low")) \u_数据块副本_21  (
    .D(BlockDataIn_3), .en(and_5_out), .Q(\数据块副本_21_q ), .clk(CLK));  // open: clr
  assign SlotData2 = L4 ? \数据块副本_21_q  : 32'bz;  // Controlled_Buffer controlled_buffer_37
  assign SlotData2 = L5 ? \数据块副本_22_q  : 32'bz;  // Controlled_Buffer controlled_buffer_38
  Register #(.width(32), .trigger("rising"), .Select("low")) \u_数据块副本_22  (
    .D(BlockDataIn_3), .en(and_6_out), .Q(\数据块副本_22_q ), .clk(CLK));  // open: clr
  Register #(.width(32), .trigger("rising"), .Select("low")) \u_数据块副本_23  (
    .D(BlockDataIn_3), .en(and_7_out), .Q(\数据块副本_23_q ), .clk(CLK));  // open: clr
  assign SlotData2 = L6 ? \数据块副本_23_q  : 32'bz;  // Controlled_Buffer controlled_buffer_39
  assign SlotData2 = L7 ? \数据块副本_24_q  : 32'bz;  // Controlled_Buffer controlled_buffer_40
  Register #(.width(32), .trigger("rising"), .Select("low")) \u_数据块副本_24  (
    .D(BlockDataIn_3), .en(and_8_out), .Q(\数据块副本_24_q ), .clk(CLK));  // open: clr
  Register #(.width(32), .trigger("rising"), .Select("low")) \u_数据块副本_25  (
    .D(BlockDataIn_4), .en(and_1_out), .Q(\数据块副本_25_q ), .clk(CLK));  // open: clr
  assign SlotData3 = L0 ? \数据块副本_25_q  : 32'bz;  // Controlled_Buffer controlled_buffer_41
  Register #(.width(32), .trigger("rising"), .Select("low")) \u_数据块副本_26  (
    .D(BlockDataIn_4), .en(and_2_out), .Q(\数据块副本_26_q ), .clk(CLK));  // open: clr
  assign SlotData3 = L1 ? \数据块副本_26_q  : 32'bz;  // Controlled_Buffer controlled_buffer_42
  assign SlotData3 = L2 ? \数据块副本_27_q  : 32'bz;  // Controlled_Buffer controlled_buffer_43
  Register #(.width(32), .trigger("rising"), .Select("low")) \u_数据块副本_27  (
    .D(BlockDataIn_4), .en(and_3_out), .Q(\数据块副本_27_q ), .clk(CLK));  // open: clr
  Register #(.width(32), .trigger("rising"), .Select("low")) \u_数据块副本_28  (
    .D(BlockDataIn_4), .en(and_4_out), .Q(\数据块副本_28_q ), .clk(CLK));  // open: clr
  assign SlotData3 = L3 ? \数据块副本_28_q  : 32'bz;  // Controlled_Buffer controlled_buffer_44
  assign SlotData3 = L4 ? \数据块副本_29_q  : 32'bz;  // Controlled_Buffer controlled_buffer_45
  Register #(.width(32), .trigger("rising"), .Select("low")) \u_数据块副本_29  (
    .D(BlockDataIn_4), .en(and_5_out), .Q(\数据块副本_29_q ), .clk(CLK));  // open: clr
  assign SlotData3 = L5 ? \数据块副本_30_q  : 32'bz;  // Controlled_Buffer controlled_buffer_46
  Register #(.width(32), .trigger("rising"), .Select("low")) \u_数据块副本_30  (
    .D(BlockDataIn_4), .en(and_6_out), .Q(\数据块副本_30_q ), .clk(CLK));  // open: clr
  Register #(.width(32), .trigger("rising"), .Select("low")) \u_数据块副本_31  (
    .D(BlockDataIn_4), .en(and_7_out), .Q(\数据块副本_31_q ), .clk(CLK));  // open: clr
  assign SlotData3 = L6 ? \数据块副本_31_q  : 32'bz;  // Controlled_Buffer controlled_buffer_47
  Register #(.width(32), .trigger("rising"), .Select("low")) \u_数据块副本_32  (
    .D(BlockDataIn_4), .en(and_8_out), .Q(\数据块副本_32_q ), .clk(CLK));  // open: clr
  assign SlotData3 = L7 ? \数据块副本_32_q  : 32'bz;  // Controlled_Buffer controlled_buffer_48
  and and_1 (and_1_out, L0, BlkDataReady);
  and and_2 (and_2_out, L1, BlkDataReady);
  and and_3 (and_3_out, L2, BlkDataReady);
  and and_4 (and_4_out, L3, BlkDataReady);
  and and_5 (and_5_out, L4, BlkDataReady);
  and and_6 (and_6_out, L5, BlkDataReady);
  and and_7 (and_7_out, L6, BlkDataReady);
  and and_8 (and_8_out, L7, BlkDataReady);

  // Other names for the same wires on the sheet: Blk0[31:0] = BlockDataIn; Blk1[31:0] = BlockDataIn_2;
  //   Blk2[31:0] = BlockDataIn_3; Blk3[31:0] = BlockDataIn_4; BlkReady = BlkDataReady; Offset[1:0] = Addr[1:0];
  //   字节地址[15:0] = Addr; Tag[10:0] = Addr[15:5]

  // Notes on the sheet:
  //   16位
  //   输入引脚区
  //   标记位
  //   有效位
  //   三态门控制多行输出
  //   行选中
  //   标记位
  //   有效位
  //   三态门控制多行输出
  //   行选中
  //   标记位
  //   有效位
  //   三态门控制多行输出
  //   行选中
  //   标记位
  //   有效位
  //   三态门控制多行输出
  //   行选中
  //   标记位
  //   有效位
  //   三态门控制多行输出
  //   行选中
  //   标记位
  //   有效位
  //   三态门控制多行输出
  //   行选中
  //   标记位
  //   有效位
  //   三态门控制多行输出
  //   行选中
  //   有效位
  //   三态门控制多行输出
  //   行选中
  //   电路功能：利用上面给定的隧道构建8行的Cache
  //   标记位
  //   请在下方利用上方输入输出引脚的隧道信号构建电路，ctrl+d复制选择部件
  //   请勿增改引脚，请勿修改子电路封装
  //   块数据输出
  //   块数据输出
  //   块数据输出
  //   块数据输出
  //   块数据输出
  //   块数据输出
  //   块数据输出
  //   块数据输出
  //   块数据输出
  //   块数据输出
  //   块数据输出
  //   块数据输出
  //   块数据输出
  //   块数据输出
  //   块数据输出
  //   块数据输出
  //   块数据输出
  //   块数据输出
  //   块数据输出
  //   块数据输出
  //   块数据输出
  //   块数据输出
  //   块数据输出
  //   块数据输出
  //   输出引脚区
  //   cache行0
  //   块数据输出
  //   cache行1
  //   块数据输出
  //   cache行2
  //   块数据输出
  //   cache行3
  //   块数据输出
  //   cache行4
  //   块数据输出
  //   cache行5
  //   块数据输出
  //   cache行6
  //   块数据输出
  //   cache行7
  //   块数据输出
endmodule

module ExChange_logic (
  input  [15:0] Addr,
  input  [31:0] ByteDataIn,
  input  Miss,
  input  Enable,
  input  CLK,
  output [15:0] ByteAddrOut,
  output [31:0] BlockDataIn0,
  output [31:0] BlockDataIn1,
  output [31:0] BlockDataIn2,
  output [31:0] BlockDataIn3,
  output BlkDataReady
);

  wire FSM_byte0_ready, FSM_byte1_ready, FSM_byte2_ready, FSM_byte3_ready;
  wire [31:0] register_1_q, register_2_q, register_3_q, register_4_q;

  assign ByteAddrOut = FSM_byte0_ready ? {Addr[15:2], 2'b00} : 16'bz;  // Controlled_Buffer controlled_buffer_1
  ExChange_FSM FSM (
    .Clk(CLK), .Miss(Miss), .Byte0_Ready(FSM_byte0_ready), .Byte1_Ready(FSM_byte1_ready),
    .Byte2_Ready(FSM_byte2_ready), .Byte3_Ready(FSM_byte3_ready), .Byte0_Ready_2(BlkDataReady), .En(Enable));
  assign ByteAddrOut = FSM_byte1_ready ? {Addr[15:2], 2'b01} : 16'bz;  // Controlled_Buffer controlled_buffer_2
  assign ByteAddrOut = FSM_byte2_ready ? {Addr[15:2], 2'b10} : 16'bz;  // Controlled_Buffer controlled_buffer_3
  assign ByteAddrOut = FSM_byte3_ready ? {Addr[15:2], 2'b11} : 16'bz;  // Controlled_Buffer controlled_buffer_4
  Register #(.width(32), .trigger("rising"), .Select("low")) register_1 (
    .D(ByteDataIn), .en(FSM_byte0_ready), .Q(register_1_q), .clk(CLK));  // open: clr
  Register #(.width(32), .trigger("rising"), .Select("low")) register_2 (
    .D(ByteDataIn), .en(FSM_byte1_ready), .Q(register_2_q), .clk(CLK));  // open: clr
  Register #(.width(32), .trigger("rising"), .Select("low")) register_3 (
    .D(ByteDataIn), .en(FSM_byte2_ready), .Q(register_3_q), .clk(CLK));  // open: clr
  Register #(.width(32), .trigger("rising"), .Select("low")) register_4 (
    .D(ByteDataIn), .en(FSM_byte3_ready), .Q(register_4_q), .clk(CLK));  // open: clr
  assign BlockDataIn0 = BlkDataReady ? register_1_q : 32'bz;  // Controlled_Buffer controlled_buffer_5
  assign BlockDataIn1 = BlkDataReady ? register_2_q : 32'bz;  // Controlled_Buffer controlled_buffer_6
  assign BlockDataIn2 = BlkDataReady ? register_3_q : 32'bz;  // Controlled_Buffer controlled_buffer_7
  assign BlockDataIn3 = BlkDataReady ? register_4_q : 32'bz;  // Controlled_Buffer controlled_buffer_8

  // Notes on the sheet:
  //   数据缓存寄存器
endmodule

module ExChange_FSM (
  input  En,
  input  Clk,
  input  Miss,
  output Byte0_Ready,
  output Byte1_Ready,
  output Byte2_Ready,
  output Byte3_Ready,
  output Byte0_Ready_2
);

  wire and_1_out, and_2_out, and_3_out, and_4_out, and_5_out, and_6_out, and_7_out, Next_Q0, Next_Q1,
       Next_Q2, Next_Q3, not_1_out, not_2_out, not_3_out, not_4_out, not_5_out, not_6_out, not_7_out,
       not_8_out, not_9_out, not_10_out, not_11_out, not_12_out, not_13_out, or_1_out, or_2_out, Q0, Q1, Q2,
       Q3;

  not not_1 (not_1_out, Q3);
  not not_2 (not_2_out, Q3);
  not not_3 (not_3_out, Q2);
  not not_4 (not_4_out, Q3);
  not not_5 (not_5_out, Q1);
  not not_6 (not_6_out, Q3);
  not not_7 (not_7_out, Q0);
  not not_8 (not_8_out, Q3);
  not not_9 (not_9_out, Q0);
  D_Flip_Flop #(.trigger("rising"), .Pre_Clr_Positions("LEGACY"), .NegatePresetClear("false"), .enable("true"), .NewFFLayout("false")) d_ff_1 (
    .clk(Clk), .D(Next_Q3), .Q(Q3), .en(En));  // open: Qn, preset, reset
  D_Flip_Flop #(.trigger("rising"), .Pre_Clr_Positions("LEGACY"), .NegatePresetClear("false"), .enable("true"), .NewFFLayout("false")) d_ff_2 (
    .clk(Clk), .D(Next_Q2), .Q(Q2), .en(En));  // open: Qn, preset, reset
  D_Flip_Flop #(.trigger("rising"), .Pre_Clr_Positions("LEGACY"), .NegatePresetClear("false"), .enable("true"), .NewFFLayout("false")) d_ff_3 (
    .clk(Clk), .D(Next_Q1), .Q(Q1), .en(En));  // open: Qn, preset, reset
  D_Flip_Flop #(.trigger("rising"), .Pre_Clr_Positions("LEGACY"), .NegatePresetClear("false"), .enable("true"), .NewFFLayout("false")) d_ff_4 (
    .clk(Clk), .D(Next_Q0), .Q(Q0), .en(En));  // open: Qn, preset, reset
  and and_1 (and_1_out, not_1_out, Q2, Q1, Q0);
  and and_2 (and_2_out, not_2_out, not_3_out, Q1, Q0);
  not not_10 (not_10_out, Q3);
  and and_3 (and_3_out, not_10_out, Q2, not_11_out);
  not not_11 (not_11_out, Q1);
  not not_12 (not_12_out, Q3);
  and and_4 (and_4_out, not_12_out, Q2, not_13_out);
  not not_13 (not_13_out, Q0);
  and and_5 (and_5_out, not_4_out, not_5_out, Q0);
  and and_6 (and_6_out, not_6_out, Q1, not_7_out);
  and and_7 (and_7_out, not_8_out, not_9_out);
  or or_1 (or_1_out, and_2_out, and_3_out, and_4_out);
  or or_2 (or_2_out, and_5_out, and_6_out);
  Decoder #(.select(4), .tristate("false"), .disabled(0), .enable("false")) decoder_1 (
    .out1(Byte0_Ready), .out3(Byte1_Ready), .out5(Byte2_Ready), .out7(Byte3_Ready), .out8(Byte0_Ready_2),
    .sel({Q3, Q2, Q1, Q0}));  // open: out0, out2, out4, out6, out9, out10, out11, out12, out13, out14, out15
  and and_8 (Next_Q3, and_1_out, Miss);
  and and_9 (Next_Q2, or_1_out, Miss);
  and and_10 (Next_Q1, Miss, or_2_out);
  and and_11 (Next_Q0, Miss, and_7_out);
endmodule
module \Cache全相联_LRU  (
  input  [31:0] BlockDataIn,
  input  [31:0] BlockDataIn_2,
  input  [31:0] BlockDataIn_3,
  input  [31:0] BlockDataIn_4,
  input  [15:0] Addr,
  input  BlkDataReady,
  input  CLK,
  output Miss,
  output [31:0] DataOut
);

  wire and_1_out, and_2_out, and_3_out, and_4_out, and_5_out, and_6_out, and_7_out, and_8_out,
       comparator_1_lt, comparator_2_lt, comparator_3_lt, comparator_4_lt, comparator_5_lt, comparator_6_lt,
       comparator_7_eq, comparator_8_eq, comparator_9_eq, comparator_10_eq, comparator_11_eq,
       comparator_12_eq, comparator_13_eq, comparator_14_eq, comparator_15_lt, counter_1_carry,
       counter_2_carry, counter_3_carry, counter_4_carry, counter_5_carry, counter_6_carry, counter_7_carry,
       counter_8_carry, empty0, empty1, empty2, empty3, empty4, empty5, empty6, empty7, Hit, L0, L1, L2, L3,
       L4, L5, L6, L7, or_1_out, TL0, TL1, TL2, TL3, TL4, TL5, TL6, TL7, undriven, Valid0, Valid1, Valid2,
       Valid3, Valid4, Valid5, Valid6, Valid7, VALID_2_q, VALID_3_q, VALID_4_q, VALID_5_q, VALID_6_q,
       VALID_7_q, VALID_8_q, VALID_q;
  wire [13:0] TagData0, TagData1, TagData2, TagData3, TagData4, TagData5, TagData6, TagData7;
  wire [28:0] C0, C1, C2, C3, C4, C5, C6, C7, counter_1_q, counter_2_q, counter_3_q, counter_4_q,
       counter_5_q, counter_6_q, counter_7_q, counter_8_q;
  wire [31:0] multiplexer_2_out, multiplexer_3_out, multiplexer_4_out, multiplexer_5_out, multiplexer_6_out,
       multiplexer_7_out, multiplexer_8_out, SlotData0, SlotData1, SlotData2, SlotData3, \数据块副本_2_q ,
       \数据块副本_3_q , \数据块副本_4_q , \数据块副本_5_q , \数据块副本_6_q , \数据块副本_7_q , \数据块副本_8_q , \数据块副本_9_q ,
       \数据块副本_10_q , \数据块副本_11_q , \数据块副本_12_q , \数据块副本_13_q , \数据块副本_14_q , \数据块副本_15_q , \数据块副本_16_q ,
       \数据块副本_17_q , \数据块副本_18_q , \数据块副本_19_q , \数据块副本_20_q , \数据块副本_21_q , \数据块副本_22_q , \数据块副本_23_q ,
       \数据块副本_24_q , \数据块副本_25_q , \数据块副本_26_q , \数据块副本_27_q , \数据块副本_28_q , \数据块副本_29_q , \数据块副本_30_q ,
       \数据块副本_31_q , \数据块副本_32_q , \数据块副本_q ;

  Register #(.width(1), .trigger("rising"), .Select("low")) register_1 (
    .D(1'b1), .Q(empty0), .clk(Valid0));  // open: en, clr
  // Probe on Addr[15:2]
  assign Valid0 = L0 ? VALID_q : 1'bz;  // Controlled_Buffer controlled_buffer_1
  Register #(.width(1), .trigger("rising"), .Select("low")) VALID (
    .D(1'b1), .en(and_1_out), .Q(VALID_q), .clk(CLK));  // open: clr
  Register #(.width(1), .trigger("rising"), .Select("low")) VALID_2 (
    .D(1'b1), .en(and_2_out), .Q(VALID_2_q), .clk(CLK));  // open: clr
  assign Valid1 = L1 ? VALID_2_q : 1'bz;  // Controlled_Buffer controlled_buffer_2
  Register #(.width(1), .trigger("rising"), .Select("low")) VALID_3 (
    .D(1'b1), .en(and_3_out), .Q(VALID_3_q), .clk(CLK));  // open: clr
  assign Valid2 = L2 ? VALID_3_q : 1'bz;  // Controlled_Buffer controlled_buffer_3
  Register #(.width(1), .trigger("rising"), .Select("low")) VALID_4 (
    .D(1'b1), .en(and_4_out), .Q(VALID_4_q), .clk(CLK));  // open: clr
  assign Valid3 = L3 ? VALID_4_q : 1'bz;  // Controlled_Buffer controlled_buffer_4
  assign Valid4 = L4 ? VALID_5_q : 1'bz;  // Controlled_Buffer controlled_buffer_5
  Register #(.width(1), .trigger("rising"), .Select("low")) VALID_5 (
    .D(1'b1), .en(and_5_out), .Q(VALID_5_q), .clk(CLK));  // open: clr
  Register #(.width(1), .trigger("rising"), .Select("low")) VALID_6 (
    .D(1'b1), .en(and_6_out), .Q(VALID_6_q), .clk(CLK));  // open: clr
  assign Valid5 = L5 ? VALID_6_q : 1'bz;  // Controlled_Buffer controlled_buffer_6
  assign Valid6 = L6 ? VALID_7_q : 1'bz;  // Controlled_Buffer controlled_buffer_7
  Register #(.width(1), .trigger("rising"), .Select("low")) VALID_7 (
    .D(1'b1), .en(and_7_out), .Q(VALID_7_q), .clk(CLK));  // open: clr
  Register #(.width(1), .trigger("rising"), .Select("low")) VALID_8 (
    .D(1'b1), .en(and_8_out), .Q(VALID_8_q), .clk(CLK));  // open: clr
  assign Valid7 = L7 ? VALID_8_q : 1'bz;  // Controlled_Buffer controlled_buffer_8
  Register #(.width(1), .trigger("rising"), .Select("low")) register_2 (
    .D(1'b1), .Q(empty1), .clk(Valid1));  // open: en, clr
  Multiplexer #(.select(2), .width(32), .disabled("Z"), .enable("false")) multiplexer_1 (
    .in0(SlotData0), .in1(SlotData1), .in2(SlotData2), .in3(SlotData3), .out(DataOut), .sel(Addr[1:0]));
  Register #(.width(14), .trigger("rising"), .Select("low")) TAG (
    .D(Addr[15:2]), .en(and_1_out), .Q(TagData0), .clk(CLK));  // open: clr
  Register #(.width(14), .trigger("rising"), .Select("low")) TAG_2 (
    .D(Addr[15:2]), .en(and_2_out), .Q(TagData1), .clk(CLK));  // open: clr
  Register #(.width(14), .trigger("rising"), .Select("low")) TAG_3 (
    .D(Addr[15:2]), .en(and_3_out), .Q(TagData2), .clk(CLK));  // open: clr
  Register #(.width(14), .trigger("rising"), .Select("low")) TAG_4 (
    .D(Addr[15:2]), .en(and_4_out), .Q(TagData3), .clk(CLK));  // open: clr
  Register #(.width(14), .trigger("rising"), .Select("low")) TAG_5 (
    .D(Addr[15:2]), .en(and_5_out), .Q(TagData4), .clk(CLK));  // open: clr
  Register #(.width(14), .trigger("rising"), .Select("low")) TAG_6 (
    .D(Addr[15:2]), .en(and_6_out), .Q(TagData5), .clk(CLK));  // open: clr
  Register #(.width(14), .trigger("rising"), .Select("low")) TAG_7 (
    .D(Addr[15:2]), .en(and_7_out), .Q(TagData6), .clk(CLK));  // open: clr
  // Probe on Addr[15:2]
  Register #(.width(14), .trigger("rising"), .Select("low")) TAG_8 (
    .D(Addr[15:2]), .en(and_8_out), .Q(TagData7), .clk(CLK), .clr(CLK));
  Register #(.width(1), .trigger("rising"), .Select("low")) register_3 (
    .D(1'b1), .Q(empty2), .clk(Valid2));  // open: en, clr
  // Probe on TagData6
  // Probe on TagData7
  Register #(.width(1), .trigger("rising"), .Select("low")) register_4 (
    .D(1'b1), .Q(empty3), .clk(Valid3));  // open: en, clr
  Register #(.width(32), .trigger("rising"), .Select("low")) \u_数据块副本  (
    .D(BlockDataIn), .en(and_1_out), .Q(\数据块副本_q ), .clk(CLK));  // open: clr
  assign SlotData0 = L0 ? \数据块副本_q  : 32'bz;  // Controlled_Buffer controlled_buffer_9
  assign SlotData0 = L1 ? \数据块副本_2_q  : 32'bz;  // Controlled_Buffer controlled_buffer_10
  Register #(.width(32), .trigger("rising"), .Select("low")) \u_数据块副本_2  (
    .D(BlockDataIn), .en(and_2_out), .Q(\数据块副本_2_q ), .clk(CLK));  // open: clr
  Register #(.width(32), .trigger("rising"), .Select("low")) \u_数据块副本_3  (
    .D(BlockDataIn), .en(and_3_out), .Q(\数据块副本_3_q ), .clk(CLK));  // open: clr
  assign SlotData0 = L2 ? \数据块副本_3_q  : 32'bz;  // Controlled_Buffer controlled_buffer_11
  Register #(.width(32), .trigger("rising"), .Select("low")) \u_数据块副本_4  (
    .D(BlockDataIn), .en(and_4_out), .Q(\数据块副本_4_q ), .clk(CLK));  // open: clr
  assign SlotData0 = L3 ? \数据块副本_4_q  : 32'bz;  // Controlled_Buffer controlled_buffer_12
  Register #(.width(32), .trigger("rising"), .Select("low")) \u_数据块副本_5  (
    .D(BlockDataIn), .en(and_5_out), .Q(\数据块副本_5_q ), .clk(CLK));  // open: clr
  assign SlotData0 = L4 ? \数据块副本_5_q  : 32'bz;  // Controlled_Buffer controlled_buffer_13
  assign SlotData0 = L5 ? \数据块副本_6_q  : 32'bz;  // Controlled_Buffer controlled_buffer_14
  Register #(.width(32), .trigger("rising"), .Select("low")) \u_数据块副本_6  (
    .D(BlockDataIn), .en(and_6_out), .Q(\数据块副本_6_q ), .clk(CLK));  // open: clr
  Register #(.width(32), .trigger("rising"), .Select("low")) \u_数据块副本_7  (
    .D(BlockDataIn), .en(and_7_out), .Q(\数据块副本_7_q ), .clk(CLK));  // open: clr
  assign SlotData0 = L6 ? \数据块副本_7_q  : 32'bz;  // Controlled_Buffer controlled_buffer_15
  Register #(.width(32), .trigger("rising"), .Select("low")) \u_数据块副本_8  (
    .D(BlockDataIn), .en(and_8_out), .Q(\数据块副本_8_q ), .clk(CLK));  // open: clr
  assign SlotData0 = L7 ? \数据块副本_8_q  : 32'bz;  // Controlled_Buffer controlled_buffer_16
  Register #(.width(1), .trigger("rising"), .Select("low")) register_5 (
    .D(1'b1), .Q(empty4), .clk(Valid4));  // open: en, clr
  or or_1 (or_1_out, TL0, TL1, TL2, TL3, TL4, TL5, TL6, TL7);
  Register #(.width(1), .trigger("rising"), .Select("low")) register_6 (
    .D(1'b1), .Q(empty5), .clk(Valid5));  // open: en, clr
  assign SlotData1 = L0 ? \数据块副本_9_q  : 32'bz;  // Controlled_Buffer controlled_buffer_17
  Register #(.width(32), .trigger("rising"), .Select("low")) \u_数据块副本_9  (
    .D(BlockDataIn_2), .en(and_1_out), .Q(\数据块副本_9_q ), .clk(CLK));  // open: clr
  assign SlotData1 = L1 ? \数据块副本_10_q  : 32'bz;  // Controlled_Buffer controlled_buffer_18
  Register #(.width(32), .trigger("rising"), .Select("low")) \u_数据块副本_10  (
    .D(BlockDataIn_2), .en(and_2_out), .Q(\数据块副本_10_q ), .clk(CLK));  // open: clr
  Register #(.width(32), .trigger("rising"), .Select("low")) \u_数据块副本_11  (
    .D(BlockDataIn_2), .en(and_3_out), .Q(\数据块副本_11_q ), .clk(CLK));  // open: clr
  assign SlotData1 = L2 ? \数据块副本_11_q  : 32'bz;  // Controlled_Buffer controlled_buffer_19
  Register #(.width(32), .trigger("rising"), .Select("low")) \u_数据块副本_12  (
    .D(BlockDataIn_2), .en(and_4_out), .Q(\数据块副本_12_q ), .clk(CLK));  // open: clr
  assign SlotData1 = L3 ? \数据块副本_12_q  : 32'bz;  // Controlled_Buffer controlled_buffer_20
  assign SlotData1 = L4 ? \数据块副本_13_q  : 32'bz;  // Controlled_Buffer controlled_buffer_21
  Register #(.width(32), .trigger("rising"), .Select("low")) \u_数据块副本_13  (
    .D(BlockDataIn_2), .en(and_5_out), .Q(\数据块副本_13_q ), .clk(CLK));  // open: clr
  Register #(.width(32), .trigger("rising"), .Select("low")) \u_数据块副本_14  (
    .D(BlockDataIn_2), .en(and_6_out), .Q(\数据块副本_14_q ), .clk(CLK));  // open: clr
  assign SlotData1 = L5 ? \数据块副本_14_q  : 32'bz;  // Controlled_Buffer controlled_buffer_22
  Register #(.width(32), .trigger("rising"), .Select("low")) \u_数据块副本_15  (
    .D(BlockDataIn_2), .en(and_7_out), .Q(\数据块副本_15_q ), .clk(CLK));  // open: clr
  assign SlotData1 = L6 ? \数据块副本_15_q  : 32'bz;  // Controlled_Buffer controlled_buffer_23
  Register #(.width(32), .trigger("rising"), .Select("low")) \u_数据块副本_16  (
    .D(BlockDataIn_2), .en(and_8_out), .Q(\数据块副本_16_q ), .clk(CLK));  // open: clr
  assign SlotData1 = L7 ? \数据块副本_16_q  : 32'bz;  // Controlled_Buffer controlled_buffer_24
  nand nand_1 (Miss, or_1_out, 1'b1);
  not not_1 (Hit, Miss);
  Register #(.width(1), .trigger("rising"), .Select("low")) register_7 (
    .D(1'b1), .Q(empty6), .clk(Valid6));  // open: en, clr
  Register #(.width(32), .trigger("rising"), .Select("low")) \u_数据块副本_17  (
    .D(BlockDataIn_3), .en(and_1_out), .Q(\数据块副本_17_q ), .clk(CLK));  // open: clr
  Register #(.width(32), .trigger("rising"), .Select("low")) \u_数据块副本_18  (
    .D(BlockDataIn_3), .en(and_2_out), .Q(\数据块副本_18_q ), .clk(CLK));  // open: clr
  Register #(.width(32), .trigger("rising"), .Select("low")) \u_数据块副本_19  (
    .D(BlockDataIn_3), .en(and_3_out), .Q(\数据块副本_19_q ), .clk(CLK));  // open: clr
  Register #(.width(32), .trigger("rising"), .Select("low")) \u_数据块副本_20  (
    .D(BlockDataIn_3), .en(and_4_out), .Q(\数据块副本_20_q ), .clk(CLK));  // open: clr
  Register #(.width(32), .trigger("rising"), .Select("low")) \u_数据块副本_21  (
    .D(BlockDataIn_3), .en(and_5_out), .Q(\数据块副本_21_q ), .clk(CLK));  // open: clr
  Register #(.width(32), .trigger("rising"), .Select("low")) \u_数据块副本_22  (
    .D(BlockDataIn_3), .en(and_6_out), .Q(\数据块副本_22_q ), .clk(CLK));  // open: clr
  Register #(.width(32), .trigger("rising"), .Select("low")) \u_数据块副本_23  (
    .D(BlockDataIn_3), .en(and_7_out), .Q(\数据块副本_23_q ), .clk(CLK));  // open: clr
  assign SlotData2 = L0 ? \数据块副本_17_q  : 32'bz;  // Controlled_Buffer controlled_buffer_25
  assign SlotData2 = L1 ? \数据块副本_18_q  : 32'bz;  // Controlled_Buffer controlled_buffer_26
  assign SlotData2 = L2 ? \数据块副本_19_q  : 32'bz;  // Controlled_Buffer controlled_buffer_27
  assign SlotData2 = L3 ? \数据块副本_20_q  : 32'bz;  // Controlled_Buffer controlled_buffer_28
  assign SlotData2 = L4 ? \数据块副本_21_q  : 32'bz;  // Controlled_Buffer controlled_buffer_29
  assign SlotData2 = L5 ? \数据块副本_22_q  : 32'bz;  // Controlled_Buffer controlled_buffer_30
  assign SlotData2 = L6 ? \数据块副本_23_q  : 32'bz;  // Controlled_Buffer controlled_buffer_31
  assign SlotData2 = L7 ? \数据块副本_24_q  : 32'bz;  // Controlled_Buffer controlled_buffer_32
  Register #(.width(32), .trigger("rising"), .Select("low")) \u_数据块副本_24  (
    .D(BlockDataIn_3), .en(and_8_out), .Q(\数据块副本_24_q ), .clk(CLK));  // open: clr
  Register #(.width(1), .trigger("rising"), .Select("low")) register_8 (
    .D(1'b1), .Q(empty7), .clk(Valid7));  // open: en, clr
  Register #(.width(32), .trigger("rising"), .Select("low")) \u_数据块副本_25  (
    .D(BlockDataIn_4), .en(and_1_out), .Q(\数据块副本_25_q ), .clk(CLK));  // open: clr
  Register #(.width(32), .trigger("rising"), .Select("low")) \u_数据块副本_26  (
    .D(BlockDataIn_4), .en(and_2_out), .Q(\数据块副本_26_q ), .clk(CLK));  // open: clr
  Register #(.width(32), .trigger("rising"), .Select("low")) \u_数据块副本_27  (
    .D(BlockDataIn_4), .en(and_3_out), .Q(\数据块副本_27_q ), .clk(CLK));  // open: clr
  Register #(.width(32), .trigger("rising"), .Select("low")) \u_数据块副本_28  (
    .D(BlockDataIn_4), .en(and_4_out), .Q(\数据块副本_28_q ), .clk(CLK));  // open: clr
  Register #(.width(32), .trigger("rising"), .Select("low")) \u_数据块副本_29  (
    .D(BlockDataIn_4), .en(and_5_out), .Q(\数据块副本_29_q ), .clk(CLK));  // open: clr
  Register #(.width(32), .trigger("rising"), .Select("low")) \u_数据块副本_30  (
    .D(BlockDataIn_4), .en(and_6_out), .Q(\数据块副本_30_q ), .clk(CLK));  // open: clr
  Register #(.width(32), .trigger("rising"), .Select("low")) \u_数据块副本_31  (
    .D(BlockDataIn_4), .en(and_7_out), .Q(\数据块副本_31_q ), .clk(CLK));  // open: clr
  Register #(.width(32), .trigger("rising"), .Select("low")) \u_数据块副本_32  (
    .D(BlockDataIn_4), .en(and_8_out), .Q(\数据块副本_32_q ), .clk(CLK));  // open: clr
  assign SlotData3 = L0 ? \数据块副本_25_q  : 32'bz;  // Controlled_Buffer controlled_buffer_33
  assign SlotData3 = L1 ? \数据块副本_26_q  : 32'bz;  // Controlled_Buffer controlled_buffer_34
  assign SlotData3 = L2 ? \数据块副本_27_q  : 32'bz;  // Controlled_Buffer controlled_buffer_35
  assign SlotData3 = L3 ? \数据块副本_28_q  : 32'bz;  // Controlled_Buffer controlled_buffer_36
  assign SlotData3 = L4 ? \数据块副本_29_q  : 32'bz;  // Controlled_Buffer controlled_buffer_37
  assign SlotData3 = L5 ? \数据块副本_30_q  : 32'bz;  // Controlled_Buffer controlled_buffer_38
  assign SlotData3 = L6 ? \数据块副本_31_q  : 32'bz;  // Controlled_Buffer controlled_buffer_39
  assign SlotData3 = L7 ? \数据块副本_32_q  : 32'bz;  // Controlled_Buffer controlled_buffer_40
  and and_1 (and_1_out, L0, BlkDataReady);
  and and_2 (and_2_out, L1, BlkDataReady);
  and and_3 (and_3_out, L2, BlkDataReady);
  and and_4 (and_4_out, L3, BlkDataReady);
  and and_5 (and_5_out, L4, BlkDataReady);
  and and_6 (and_6_out, L5, BlkDataReady);
  and and_7 (and_7_out, L6, BlkDataReady);
  and and_8 (and_8_out, L7, BlkDataReady);
  // Probe on C0
  Comparator #(.width(32), .mode("unsigned")) comparator_1 (
    .a({C0, 3'b000}), .b({C1, 3'b001}), .lt(comparator_1_lt));  // open: gt, eq
  Comparator #(.width(32), .mode("unsigned")) comparator_2 (
    .a({C2, 3'b010}), .b({C3, 3'b011}), .lt(comparator_2_lt));  // open: gt, eq
  Comparator #(.width(32), .mode("unsigned")) comparator_3 (
    .a({C4, 3'b100}), .b({C5, 3'b101}), .lt(comparator_3_lt));  // open: gt, eq
  Comparator #(.width(32), .mode("unsigned")) comparator_4 (
    .a({C6, 3'b110}), .b({C7, 3'b111}), .lt(comparator_4_lt));  // open: gt, eq
  Counter #(.width(29), .max('h1fffffff), .ongoal("wrap"), .trigger("rising"), .behavior("new")) counter_1 (
    .load(counter_1_carry), .D({29{1'b1}}), .Q(counter_1_q), .carry(counter_1_carry), .clk(CLK),
    .clr(and_1_out), .down(1'b0));  // open: count, preset
  Counter #(.width(29), .max('h1fffffff), .ongoal("wrap"), .trigger("rising"), .behavior("new")) counter_2 (
    .load(counter_2_carry), .D({29{1'b1}}), .Q(counter_2_q), .carry(counter_2_carry), .clk(CLK),
    .clr(and_2_out), .down(1'b0));  // open: count, preset
  Counter #(.width(29), .max('h1fffffff), .ongoal("wrap"), .trigger("rising"), .behavior("new")) counter_3 (
    .load(counter_3_carry), .D({29{1'b1}}), .Q(counter_3_q), .carry(counter_3_carry), .clk(CLK),
    .clr(and_3_out), .down(1'b0));  // open: count, preset
  Counter #(.width(29), .max('h1fffffff), .ongoal("wrap"), .trigger("rising"), .behavior("new")) counter_4 (
    .load(counter_4_carry), .D({29{1'b1}}), .Q(counter_4_q), .carry(counter_4_carry), .clk(CLK),
    .clr(and_4_out), .down(1'b0));  // open: count, preset
  Counter #(.width(29), .max('h1fffffff), .ongoal("wrap"), .trigger("rising"), .behavior("new")) counter_5 (
    .load(counter_5_carry), .D({29{1'b1}}), .Q(counter_5_q), .carry(counter_5_carry), .clk(CLK),
    .clr(and_5_out), .down(1'b0));  // open: count, preset
  Counter #(.width(29), .max('h1fffffff), .ongoal("wrap"), .trigger("rising"), .behavior("new")) counter_6 (
    .load(counter_6_carry), .D({29{1'b1}}), .Q(counter_6_q), .carry(counter_6_carry), .clk(CLK),
    .clr(and_6_out), .down(1'b0));  // open: count, preset
  Counter #(.width(29), .max('h1fffffff), .ongoal("wrap"), .trigger("rising"), .behavior("new")) counter_7 (
    .load(counter_7_carry), .D({29{1'b1}}), .Q(counter_7_q), .carry(counter_7_carry), .clk(CLK),
    .clr(and_7_out), .down(1'b0));  // open: count, preset
  Counter #(.width(29), .max('h1fffffff), .ongoal("wrap"), .trigger("rising"), .behavior("new")) counter_8 (
    .load(counter_8_carry), .D({29{1'b1}}), .Q(counter_8_q), .carry(counter_8_carry), .clk(CLK),
    .clr(and_8_out), .down(1'b0));  // open: count, preset
  Multiplexer #(.select(1), .width(32), .disabled("Z"), .enable("false")) multiplexer_2 (
    .in0({C0, 3'b000}), .in1({C1, 3'b001}), .out(multiplexer_2_out), .sel(comparator_1_lt));
  Multiplexer #(.select(1), .width(32), .disabled("Z"), .enable("false")) multiplexer_3 (
    .in0({C2, 3'b010}), .in1({C3, 3'b011}), .out(multiplexer_3_out), .sel(comparator_2_lt));
  Multiplexer #(.select(1), .width(32), .disabled("Z"), .enable("false")) multiplexer_4 (
    .in0({C4, 3'b100}), .in1({C5, 3'b101}), .out(multiplexer_4_out), .sel(comparator_3_lt));
  Multiplexer #(.select(1), .width(32), .disabled("Z"), .enable("false")) multiplexer_5 (
    .in0({C6, 3'b110}), .in1({C7, 3'b111}), .out(multiplexer_5_out), .sel(comparator_4_lt));
  Register #(.width(29), .trigger("rising"), .Select("low")) register_9 (
    .D(counter_1_q), .Q(C0), .clk(CLK));  // open: en, clr
  Register #(.width(29), .trigger("rising"), .Select("low")) register_10 (
    .D(counter_2_q), .Q(C1), .clk(CLK));  // open: en, clr
  Register #(.width(29), .trigger("rising"), .Select("low")) register_11 (
    .D(counter_3_q), .Q(C2), .clk(CLK));  // open: en, clr
  Register #(.width(29), .trigger("rising"), .Select("low")) register_12 (
    .D(counter_4_q), .Q(C3), .clk(CLK));  // open: en, clr
  Register #(.width(29), .trigger("rising"), .Select("low")) register_13 (
    .D(counter_5_q), .Q(C4), .clk(CLK));  // open: en, clr
  Register #(.width(29), .trigger("rising"), .Select("low")) register_14 (
    .D(counter_6_q), .Q(C5), .clk(CLK));  // open: en, clr
  Register #(.width(29), .trigger("rising"), .Select("low")) register_15 (
    .D(counter_7_q), .Q(C6), .clk(CLK));  // open: en, clr
  Register #(.width(29), .trigger("rising"), .Select("low")) register_16 (
    .D(counter_8_q), .Q(C7), .clk(CLK), .cs(undriven));  // open: en, clr, preset
  Comparator #(.width(32), .mode("unsigned")) comparator_5 (
    .a(multiplexer_2_out), .b(multiplexer_3_out), .lt(comparator_5_lt));  // open: gt, eq
  Comparator #(.width(32), .mode("unsigned")) comparator_6 (
    .a(multiplexer_4_out), .b(multiplexer_5_out), .lt(comparator_6_lt));  // open: gt, eq
  Multiplexer #(.select(1), .width(32), .disabled("Z"), .enable("false")) multiplexer_6 (
    .in0(multiplexer_2_out), .in1(multiplexer_3_out), .out(multiplexer_6_out), .sel(comparator_5_lt));
  Multiplexer #(.select(1), .width(32), .disabled("Z"), .enable("false")) multiplexer_7 (
    .in0(multiplexer_4_out), .in1(multiplexer_5_out), .out(multiplexer_7_out), .sel(comparator_6_lt));
  Comparator #(.width(14), .mode("twosComplement")) comparator_7 (
    .a(Addr[15:2]), .b(TagData0), .eq(comparator_7_eq));  // open: gt, lt
  Comparator #(.width(14), .mode("twosComplement")) comparator_8 (
    .a(Addr[15:2]), .b(TagData1), .eq(comparator_8_eq));  // open: gt, lt
  Comparator #(.width(14), .mode("twosComplement")) comparator_9 (
    .a(Addr[15:2]), .b(TagData2), .eq(comparator_9_eq));  // open: gt, lt
  Comparator #(.width(14), .mode("twosComplement")) comparator_10 (
    .a(Addr[15:2]), .b(TagData3), .eq(comparator_10_eq));  // open: gt, lt
  Comparator #(.width(14), .mode("twosComplement")) comparator_11 (
    .a(Addr[15:2]), .b(TagData4), .eq(comparator_11_eq));  // open: gt, lt
  Comparator #(.width(14), .mode("twosComplement")) comparator_12 (
    .a(Addr[15:2]), .b(TagData5), .eq(comparator_12_eq));  // open: gt, lt
  Comparator #(.width(14), .mode("twosComplement")) comparator_13 (
    .a(Addr[15:2]), .b(TagData6), .eq(comparator_13_eq));  // open: gt, lt
  Comparator #(.width(14), .mode("twosComplement")) comparator_14 (
    .a(Addr[15:2]), .b(TagData7), .eq(comparator_14_eq));  // open: gt, lt
  Comparator #(.width(32), .mode("unsigned")) comparator_15 (
    .a(multiplexer_6_out), .b(multiplexer_7_out), .lt(comparator_15_lt));  // open: gt, eq
  and and_9 (TL0, comparator_7_eq, empty0);
  and and_10 (TL1, comparator_8_eq, empty1);
  and and_11 (TL2, comparator_9_eq, empty2);
  and and_12 (TL3, comparator_10_eq, empty3);
  and and_13 (TL4, comparator_11_eq, empty4);
  and and_14 (TL5, comparator_12_eq, empty5);
  and and_15 (TL6, comparator_13_eq, empty6);
  and and_16 (TL7, comparator_14_eq, empty7);
  Multiplexer #(.select(1), .width(32), .disabled("Z"), .enable("false")) multiplexer_8 (
    .in0(multiplexer_6_out), .in1(multiplexer_7_out), .out(multiplexer_8_out), .sel(comparator_15_lt));
  // Probe on multiplexer_8_out[2:0]
  assign L0 = Hit ? TL0 : 1'bz;  // Controlled_Buffer controlled_buffer_41
  assign L1 = Hit ? TL1 : 1'bz;  // Controlled_Buffer controlled_buffer_42
  assign L2 = Hit ? TL2 : 1'bz;  // Controlled_Buffer controlled_buffer_43
  assign L3 = Hit ? TL3 : 1'bz;  // Controlled_Buffer controlled_buffer_44
  assign L4 = Hit ? TL4 : 1'bz;  // Controlled_Buffer controlled_buffer_45
  assign L5 = Hit ? TL5 : 1'bz;  // Controlled_Buffer controlled_buffer_46
  assign L6 = Hit ? TL6 : 1'bz;  // Controlled_Buffer controlled_buffer_47
  assign L7 = Hit ? TL7 : 1'bz;  // Controlled_Buffer controlled_buffer_48
  // Probe on L0
  Decoder #(.select(3), .tristate("false"), .disabled("Z"), .enable("true")) decoder_1 (
    .out0(L0), .out1(L1), .out2(L2), .out3(L3), .out4(L4), .out5(L5), .out6(L6), .out7(L7),
    .sel(multiplexer_8_out[2:0]), .en(Miss));
  // Probe on L7

  // Other names for the same wires on the sheet: Blk0[31:0] = BlockDataIn; Blk1[31:0] = BlockDataIn_2;
  //   Blk2[31:0] = BlockDataIn_3; Blk3[31:0] = BlockDataIn_4; BlkReady = BlkDataReady; Offset[1:0] = Addr[1:0];
  //   字节地址[15:0] = Addr; Tag[13:0] = Addr[15:2]

  // Notes on the sheet:
  //   16位
  //   输入引脚区
  //   行选中
  //   有效位
  //   行选中
  //   有效位
  //   行选中
  //   有效位
  //   行选中
  //   有效位
  //   行选中
  //   有效位
  //   行选中
  //   有效位
  //   行选中
  //   有效位
  //   行选中
  //   电路功能：利用上面给定的隧道构建8行的Cache
  //   标记位
  //   有效位
  //   三态门控制多行输出
  //   标记位
  //   三态门控制多行输出
  //   标记位
  //   三态门控制多行输出
  //   标记位
  //   三态门控制多行输出
  //   标记位
  //   三态门控制多行输出
  //   标记位
  //   三态门控制多行输出
  //   标记位
  //   三态门控制多行输出
  //   标记位
  //   三态门控制多行输出
  //   请在下方利用上方输入输出引脚的隧道信号构建电路，ctrl+d复制选择部件
  //   请勿增改引脚，请勿修改子电路封装
  //   块数据输出
  //   块数据输出
  //   块数据输出
  //   块数据输出
  //   块数据输出
  //   块数据输出
  //   块数据输出
  //   块数据输出
  //   块数据输出
  //   块数据输出
  //   块数据输出
  //   块数据输出
  //   块数据输出
  //   块数据输出
  //   块数据输出
  //   块数据输出
  //   输出引脚区
  //   块数据输出
  //   块数据输出
  //   块数据输出
  //   块数据输出
  //   块数据输出
  //   块数据输出
  //   块数据输出
  //   块数据输出
  //   cache行0
  //   块数据输出
  //   cache行1
  //   块数据输出
  //   cache行2
  //   块数据输出
  //   cache行3
  //   块数据输出
  //   cache行4
  //   块数据输出
  //   cache行5
  //   块数据输出
  //   cache行6
  //   块数据输出
  //   cache行7
  //   块数据输出
endmodule
